// Logisim project Ampliacion_Combinacional.circ as structural Verilog: 16 circuits, main circuit 7485
module _7442 (
  input  A3,
  input  A2,
  input  A1,
  input  A0,
  output Y9,
  output Y8,
  output Y7,
  output Y6,
  output Y5,
  output Y4,
  output Y3,
  output Y2,
  output Y1,
  output Y0
);

  wire not_1_out, not_2_out, not_3_out, not_4_out, not_5_out, not_6_out, not_7_out, not_8_out, not_9_out,
       not_10_out, not_11_out, not_12_out, not_13_out, not_14_out, not_15_out, not_16_out, not_17_out,
       not_18_out, not_19_out, not_20_out, not_21_out, not_22_out, not_23_out, not_24_out, not_25_out;

  not not_1 (not_1_out, A2);
  not not_2 (not_2_out, A1);
  not not_3 (not_3_out, A2);
  not not_4 (not_4_out, A1);
  not not_5 (not_5_out, A0);
  not not_6 (not_6_out, A3);
  not not_7 (not_7_out, A3);
  not not_8 (not_8_out, A0);
  not not_9 (not_9_out, A3);
  not not_10 (not_10_out, A1);
  not not_11 (not_11_out, A3);
  not not_12 (not_12_out, A1);
  not not_13 (not_13_out, A0);
  not not_14 (not_14_out, A3);
  not not_15 (not_15_out, A2);
  not not_16 (not_16_out, A3);
  not not_17 (not_17_out, A2);
  not not_18 (not_18_out, A0);
  not not_19 (not_19_out, A3);
  not not_20 (not_20_out, A2);
  not not_21 (not_21_out, A1);
  not not_22 (not_22_out, A3);
  not not_23 (not_23_out, A2);
  not not_24 (not_24_out, A1);
  not not_25 (not_25_out, A0);
  nand nand_1 (Y9, A3, not_1_out, 1'b1, not_2_out, A0);
  nand nand_2 (Y8, A3, not_3_out, 1'b1, not_4_out, not_5_out);
  nand nand_3 (Y7, not_6_out, A2, 1'b1, A1, A0);
  nand nand_4 (Y6, not_7_out, A2, 1'b1, A1, not_8_out);
  nand nand_5 (Y5, not_9_out, A2, 1'b1, not_10_out, A0);
  nand nand_6 (Y4, not_11_out, A2, 1'b1, not_12_out, not_13_out);
  nand nand_7 (Y3, not_14_out, not_15_out, 1'b1, A1, A0);
  nand nand_8 (Y2, not_16_out, not_17_out, 1'b1, A1, not_18_out);
  nand nand_9 (Y1, not_19_out, not_20_out, 1'b1, not_21_out, A0);
  nand nand_10 (Y0, not_22_out, not_23_out, 1'b1, not_24_out, not_25_out);
endmodule

module _7448 (
  input  LT,
  input  BI,
  input  RBI,
  input  D,
  input  C,
  input  B,
  input  A,
  output g,
  output f,
  output e,
  output d_2,
  output c_2,
  output b_2,
  output a_2
);

  wire and_1_out, and_2_out, and_3_out, and_4_out, and_5_out, and_6_out, and_7_out, and_8_out, and_9_out,
       and_10_out, and_11_out, and_12_out, and_13_out, and_14_out, and_15_out, and_16_out, and_17_out,
       not_1_out, not_2_out, not_3_out, not_4_out, not_5_out, not_6_out, not_7_out, not_8_out, not_9_out,
       not_10_out, not_11_out, not_12_out, not_13_out, not_14_out, not_15_out, not_16_out, not_17_out,
       not_18_out, not_19_out, not_20_out, not_21_out, not_22_out, or_1_out, or_2_out, or_3_out, or_4_out,
       or_5_out, or_6_out, or_7_out, or_8_out, or_9_out;

  not not_1 (not_1_out, BI);
  or or_1 (or_1_out, RBI, D, C, B, A);
  not not_2 (not_2_out, or_1_out);
  not not_3 (not_3_out, D);
  not not_4 (not_4_out, C);
  and and_1 (and_1_out, not_3_out, not_4_out, not_5_out);
  not not_5 (not_5_out, B);
  and and_2 (and_2_out, C, B, A);
  not not_6 (not_6_out, D);
  and and_3 (and_3_out, not_6_out, not_7_out, A);
  not not_7 (not_7_out, C);
  not not_8 (not_8_out, C);
  and and_4 (and_4_out, not_8_out, B);
  and and_5 (and_5_out, B, A);
  and and_6 (and_6_out, C, not_9_out);
  not not_9 (not_9_out, B);
  not not_10 (not_10_out, C);
  not not_11 (not_11_out, B);
  and and_7 (and_7_out, not_10_out, not_11_out, A);
  and and_8 (and_8_out, C, not_12_out, not_13_out);
  not not_12 (not_12_out, B);
  not not_13 (not_13_out, A);
  and and_9 (and_9_out, C, B, A);
  not not_14 (not_14_out, C);
  and and_10 (and_10_out, not_14_out, B, not_15_out);
  not not_15 (not_15_out, A);
  and and_11 (and_11_out, D, C);
  and and_12 (and_12_out, C, not_16_out, A);
  not not_16 (not_16_out, B);
  and and_13 (and_13_out, C, B, not_17_out);
  not not_17 (not_17_out, A);
  and and_14 (and_14_out, D, B);
  not not_18 (not_18_out, D);
  not not_19 (not_19_out, C);
  not not_20 (not_20_out, B);
  not not_21 (not_21_out, B);
  not not_22 (not_22_out, A);
  or or_2 (or_2_out, not_2_out, not_1_out);
  or or_3 (or_3_out, and_1_out, or_2_out, and_2_out);
  or or_4 (or_4_out, 1'b0, and_3_out, and_4_out, and_5_out, or_2_out);
  or or_5 (or_5_out, A, or_2_out, and_6_out);
  or or_6 (or_6_out, 1'b0, and_7_out, and_8_out, and_9_out, or_2_out);
  or or_7 (or_7_out, and_10_out, or_2_out, and_11_out);
  or or_8 (or_8_out, 1'b0, and_12_out, and_13_out, and_14_out, or_2_out);
  and and_15 (and_15_out, not_18_out, not_19_out, not_20_out, A);
  and and_16 (and_16_out, C, not_21_out, not_22_out);
  or or_9 (or_9_out, 1'b0, and_15_out, and_16_out, and_17_out, or_2_out);
  and and_17 (and_17_out, D, B);
  nand nand_1 (g, LT, or_3_out);
  nand nand_2 (f, LT, or_4_out);
  nand nand_3 (e, LT, or_5_out);
  nand nand_4 (d_2, LT, or_6_out);
  nand nand_5 (c_2, LT, or_7_out);
  nand nand_6 (b_2, LT, or_8_out);
  nand nand_7 (a_2, LT, or_9_out);

  // Notes on the sheet:
  //   BI: pull=up
endmodule

module _7483 (
  input  B3,
  input  B2,
  input  B1,
  input  B0,
  input  A3,
  input  A2,
  input  A1,
  input  A0,
  input  C0,
  output C4,
  output S3,
  output S2,
  output S1,
  output S0
);

  wire and_1_out, and_2_out, and_3_out, and_4_out, and_5_out, and_6_out, and_7_out, and_8_out, and_9_out,
       and_10_out, and_11_out, and_12_out, and_13_out, and_14_out, buffer_1_out, buffer_2_out, buffer_3_out,
       buffer_4_out, nand_1_out, nand_2_out, nand_3_out, nand_4_out, nor_1_out, nor_2_out, nor_3_out,
       nor_4_out, nor_6_out, nor_7_out, nor_8_out, not_1_out, not_2_out, not_3_out, not_4_out, not_5_out,
       not_6_out;

  nand nand_1 (nand_1_out, B3, A3);
  nor nor_1 (nor_1_out, B3, A3);
  nand nand_2 (nand_2_out, B2, A2);
  nor nor_2 (nor_2_out, B2, A2);
  nand nand_3 (nand_3_out, B1, A1);
  nor nor_3 (nor_3_out, B1, A1);
  nand nand_4 (nand_4_out, B0, A0);
  nor nor_4 (nor_4_out, B0, A0);
  not not_1 (not_1_out, C0);
  buf buffer_1 (buffer_1_out, nor_1_out);
  not not_2 (not_2_out, nor_1_out);
  buf buffer_2 (buffer_2_out, nor_2_out);
  not not_3 (not_3_out, nor_2_out);
  buf buffer_3 (buffer_3_out, nor_3_out);
  not not_4 (not_4_out, nor_3_out);
  buf buffer_4 (buffer_4_out, nor_4_out);
  not not_5 (not_5_out, nor_4_out);
  not not_6 (not_6_out, not_1_out);
  and and_1 (and_1_out, nor_2_out, nand_1_out);
  and and_2 (and_2_out, nor_3_out, nand_1_out, nand_2_out);
  and and_3 (and_3_out, nor_4_out, nand_1_out, nand_2_out, nand_3_out, 1'b1);
  and and_4 (and_4_out, nand_1_out, nand_2_out, nand_3_out, nand_4_out, not_1_out);
  and and_5 (and_5_out, nand_1_out, not_2_out);
  and and_6 (and_6_out, nor_3_out, nand_2_out);
  and and_7 (and_7_out, nor_4_out, nand_2_out, nand_3_out);
  and and_8 (and_8_out, nand_2_out, nand_3_out, nand_4_out, not_1_out, 1'b1);
  and and_9 (and_9_out, nand_2_out, not_3_out);
  and and_10 (and_10_out, nor_4_out, nand_3_out);
  and and_11 (and_11_out, nand_3_out, nand_4_out, not_1_out);
  and and_12 (and_12_out, nand_3_out, not_4_out);
  and and_13 (and_13_out, nand_4_out, not_1_out);
  and and_14 (and_14_out, nand_4_out, not_5_out);
  nor nor_5 (C4, buffer_1_out, and_1_out, and_2_out, and_3_out, and_4_out);
  xor xor_1 (S3, and_5_out, nor_6_out);
  nor nor_6 (nor_6_out, 1'b0, buffer_2_out, and_6_out, and_7_out, and_8_out);
  xor xor_2 (S2, and_9_out, nor_7_out);
  nor nor_7 (nor_7_out, buffer_3_out, and_10_out, and_11_out);
  xor xor_3 (S1, and_12_out, nor_8_out);
  nor nor_8 (nor_8_out, buffer_4_out, and_13_out);
  xor xor_4 (S0, and_14_out, not_6_out);
endmodule

module _7485 (
  input  A3,
  input  A2,
  input  A1,
  input  A0,
  input  IA_B,
  input  IA_B_2,
  input  IA_B_3,
  input  B3,
  input  B2,
  input  B1,
  input  B0,
  output A_B,
  output A_B_2,
  output A_B_3
);

  wire and_1_out, and_2_out, and_3_out, and_4_out, and_5_out, and_6_out, and_7_out, and_8_out, and_9_out,
       and_10_out, and_11_out, and_12_out, and_13_out, and_14_out, and_15_out, and_16_out, and_17_out,
       and_18_out, and_19_out, and_20_out, nand_1_out, nand_2_out, nand_3_out, nand_4_out, nor_1_out,
       nor_2_out, nor_3_out, nor_4_out;

  nand nand_1 (nand_1_out, A3, B3);
  nand nand_2 (nand_2_out, A2, B2);
  nand nand_3 (nand_3_out, A1, B1);
  nand nand_4 (nand_4_out, A0, B0);
  and and_1 (and_1_out, A3, nand_1_out);
  and and_2 (and_2_out, nand_1_out, B3);
  and and_3 (and_3_out, A2, nand_2_out);
  and and_4 (and_4_out, nand_2_out, B2);
  and and_5 (and_5_out, A1, nand_3_out);
  and and_6 (and_6_out, nand_3_out, B1);
  and and_7 (and_7_out, A0, nand_4_out);
  and and_8 (and_8_out, nand_4_out, B0);
  nor nor_1 (nor_1_out, and_1_out, and_2_out);
  nor nor_2 (nor_2_out, and_3_out, and_4_out);
  nor nor_3 (nor_3_out, and_5_out, and_6_out);
  nor nor_4 (nor_4_out, and_7_out, and_8_out);
  and and_9 (and_9_out, B3, nand_1_out);
  and and_10 (and_10_out, B2, nand_2_out, nor_1_out);
  and and_11 (and_11_out, B1, nand_3_out, nor_1_out, nor_2_out, 1'b1);
  and and_12 (and_12_out, B0, nand_4_out, nor_1_out, nor_2_out, nor_3_out);
  and and_13 (and_13_out, nor_1_out, nor_2_out, nor_3_out, nor_4_out, IA_B_3);
  and and_14 (and_14_out, nor_1_out, nor_2_out, nor_3_out, nor_4_out, IA_B_2);
  and and_15 (and_15_out, IA_B_2, nor_4_out, nor_3_out, nor_2_out, nor_1_out);
  and and_16 (and_16_out, IA_B, nor_4_out, nor_2_out, nor_3_out, nor_1_out);
  and and_17 (and_17_out, nor_3_out, nor_2_out, nor_1_out, nand_4_out, A0);
  and and_18 (and_18_out, 1'b1, nor_2_out, nor_1_out, nand_3_out, A1);
  and and_19 (and_19_out, nor_1_out, nand_2_out, A2);
  and and_20 (and_20_out, nand_1_out, A3);
  nor nor_5 (A_B, and_9_out, and_10_out, and_11_out, and_12_out, and_13_out, and_14_out, 1'b0);
  and and_21 (A_B_2, nor_1_out, nor_2_out, IA_B_2, nor_3_out, nor_4_out);
  nor nor_6 (A_B_3, and_15_out, and_16_out, and_17_out, and_18_out, and_19_out, and_20_out, 1'b0);
endmodule

module _74138 (
  input  E2,
  input  E1,
  input  E0,
  input  A2,
  input  A1,
  input  A0,
  output Y7,
  output Y6,
  output Y5,
  output Y4,
  output Y3,
  output Y2,
  output Y1,
  output Y0
);

  wire not_1_out, not_2_out, not_3_out, not_4_out, not_5_out, not_6_out, not_7_out, not_8_out, not_9_out,
       not_10_out, not_11_out, not_12_out, not_13_out, not_14_out, not_15_out, not_16_out, not_17_out,
       not_18_out, not_19_out, not_20_out, not_21_out, not_22_out, not_23_out, not_24_out, not_25_out,
       not_26_out, not_27_out, not_28_out;

  not not_1 (not_1_out, E1);
  not not_2 (not_2_out, E0);
  not not_3 (not_3_out, E1);
  not not_4 (not_4_out, E0);
  not not_5 (not_5_out, A0);
  not not_6 (not_6_out, E1);
  not not_7 (not_7_out, E0);
  not not_8 (not_8_out, A1);
  not not_9 (not_9_out, E1);
  not not_10 (not_10_out, E0);
  not not_11 (not_11_out, A1);
  not not_12 (not_12_out, A0);
  not not_13 (not_13_out, E1);
  not not_14 (not_14_out, E0);
  not not_15 (not_15_out, A2);
  not not_16 (not_16_out, E1);
  not not_17 (not_17_out, E0);
  not not_18 (not_18_out, A2);
  not not_19 (not_19_out, A0);
  not not_20 (not_20_out, E1);
  not not_21 (not_21_out, E0);
  not not_22 (not_22_out, A2);
  not not_23 (not_23_out, A1);
  not not_24 (not_24_out, E1);
  not not_25 (not_25_out, E0);
  not not_26 (not_26_out, A2);
  not not_27 (not_27_out, A1);
  not not_28 (not_28_out, A0);
  nand nand_1 (Y7, E2, not_1_out, not_2_out, 1'b1, A2, A1, A0);
  nand nand_2 (Y6, E2, not_3_out, not_4_out, 1'b1, A2, A1, not_5_out);
  nand nand_3 (Y5, E2, not_6_out, not_7_out, 1'b1, A2, not_8_out, A0);
  nand nand_4 (Y4, E2, not_9_out, not_10_out, 1'b1, A2, not_11_out, not_12_out);
  nand nand_5 (Y3, E2, not_13_out, not_14_out, 1'b1, not_15_out, A1, A0);
  nand nand_6 (Y2, E2, not_16_out, not_17_out, 1'b1, not_18_out, A1, not_19_out);
  nand nand_7 (Y1, E2, not_20_out, not_21_out, 1'b1, not_22_out, not_23_out, A0);
  nand nand_8 (Y0, E2, not_24_out, not_25_out, 1'b1, not_26_out, not_27_out, not_28_out);
endmodule

module _74139 (
  input  E,
  input  A1,
  input  A0,
  output Y3,
  output Y2,
  output Y1,
  output Y0
);

  wire not_1_out, not_2_out, not_3_out, not_4_out;

  not not_1 (not_1_out, A1);
  not not_2 (not_2_out, A0);
  not not_3 (not_3_out, A1);
  not not_4 (not_4_out, A0);
  or or_1 (Y0, A0, A1, E);
  or or_2 (Y3, not_1_out, not_2_out, E);
  or or_3 (Y2, not_3_out, A0, E);
  or or_4 (Y1, not_4_out, A1, E);
endmodule

module _74148 (
  input  I7,
  input  I6,
  input  I5,
  input  I4,
  input  I3,
  input  I2,
  input  I1,
  input  I0,
  input  EI,
  output E0,
  output GS,
  output A2,
  output A1,
  output A0
);

  wire and_1_out, and_2_out, and_3_out, and_4_out, and_5_out, and_6_out, and_7_out, and_8_out, and_9_out,
       and_10_out, and_11_out, and_12_out, not_1_out, not_2_out, not_3_out, not_4_out, not_5_out, not_6_out,
       not_7_out, not_8_out, not_9_out, not_10_out, not_11_out, not_12_out;

  not not_1 (not_1_out, I1);
  not not_2 (not_2_out, I2);
  not not_3 (not_3_out, not_2_out);
  not not_4 (not_4_out, I3);
  not not_5 (not_5_out, not_6_out);
  not not_6 (not_6_out, I4);
  not not_7 (not_7_out, I5);
  not not_8 (not_8_out, not_7_out);
  not not_9 (not_9_out, I6);
  not not_10 (not_10_out, not_9_out);
  not not_11 (not_11_out, I7);
  not not_12 (not_12_out, EI);
  and and_1 (and_1_out, not_1_out, not_3_out, not_5_out, not_10_out, not_12_out);
  and and_2 (and_2_out, not_4_out, not_5_out, not_10_out, not_12_out, 1'b1);
  and and_3 (and_3_out, not_7_out, not_10_out, not_12_out);
  and and_4 (and_4_out, not_11_out, not_12_out);
  and and_5 (and_5_out, not_2_out, not_5_out, not_8_out, not_12_out, 1'b1);
  and and_6 (and_6_out, not_4_out, not_5_out, not_8_out, not_12_out, 1'b1);
  and and_7 (and_7_out, not_9_out, not_12_out);
  and and_8 (and_8_out, not_11_out, not_12_out);
  and and_9 (and_9_out, not_6_out, not_12_out);
  and and_10 (and_10_out, not_7_out, not_12_out);
  and and_11 (and_11_out, not_9_out, not_12_out);
  and and_12 (and_12_out, not_11_out, not_12_out);
  nand nand_1 (E0, I0, I1, I2, I3, I4, I5, I6, I7, not_12_out);
  nand nand_2 (GS, E0, not_12_out);
  nor nor_1 (A0, and_1_out, and_2_out, and_3_out, and_4_out, 1'b0);
  nor nor_2 (A1, and_5_out, and_6_out, and_7_out, and_8_out, 1'b0);
  nor nor_3 (A2, and_9_out, and_10_out, and_11_out, and_12_out, 1'b0);
endmodule

module _74151 (
  input  E,
  input  S2,
  input  S1,
  input  S0,
  input  I7,
  input  I6,
  input  I5,
  input  I4,
  input  I3,
  input  I2,
  input  I1,
  input  I0,
  output Y,
  output Yn
);

  wire and_1_out, and_2_out, and_3_out, and_4_out, and_5_out, and_6_out, and_7_out, and_8_out, not_1_out,
       not_2_out, not_3_out, not_4_out, not_5_out, not_6_out, not_7_out, not_8_out, not_9_out, not_10_out,
       not_11_out, not_12_out, not_13_out, not_14_out, not_15_out, not_16_out, not_17_out, not_18_out,
       not_19_out, not_20_out;

  not not_1 (not_1_out, S2);
  not not_2 (not_2_out, S1);
  not not_3 (not_3_out, S0);
  not not_4 (not_4_out, E);
  not not_5 (not_5_out, S2);
  not not_6 (not_6_out, S1);
  not not_7 (not_7_out, E);
  not not_8 (not_8_out, S2);
  not not_9 (not_9_out, S0);
  not not_10 (not_10_out, E);
  not not_11 (not_11_out, S2);
  not not_12 (not_12_out, E);
  not not_13 (not_13_out, S1);
  not not_14 (not_14_out, S0);
  not not_15 (not_15_out, E);
  not not_16 (not_16_out, S1);
  not not_17 (not_17_out, E);
  not not_18 (not_18_out, S0);
  not not_19 (not_19_out, E);
  not not_20 (not_20_out, E);
  and and_1 (and_1_out, not_1_out, not_2_out, not_3_out, not_4_out, I0);
  and and_2 (and_2_out, not_5_out, not_6_out, S0, not_7_out, I1);
  and and_3 (and_3_out, not_8_out, S1, not_9_out, not_10_out, I2);
  and and_4 (and_4_out, not_11_out, S1, S0, not_12_out, I3);
  and and_5 (and_5_out, S2, not_13_out, not_14_out, not_15_out, I4);
  and and_6 (and_6_out, S2, not_16_out, S0, not_17_out, I5);
  and and_7 (and_7_out, S2, S1, not_18_out, not_19_out, I6);
  and and_8 (and_8_out, S2, S1, S0, not_20_out, I7);
  or or_1 (Y, and_1_out, and_2_out, and_3_out, and_4_out, 1'b0, and_5_out, and_6_out, and_7_out, and_8_out);
  not not_21 (Yn, Y);
endmodule

module _74153 (
  input  E,
  input  S1,
  input  S0,
  input  I3,
  input  I2,
  input  I1,
  input  I0,
  output Y
);

  wire and_1_out, and_2_out, and_3_out, and_4_out, not_1_out, not_2_out, not_3_out, not_4_out, not_5_out,
       not_6_out, not_7_out, not_8_out;

  not not_1 (not_1_out, S1);
  not not_2 (not_2_out, S0);
  not not_3 (not_3_out, E);
  not not_4 (not_4_out, S1);
  not not_5 (not_5_out, E);
  not not_6 (not_6_out, S0);
  not not_7 (not_7_out, E);
  not not_8 (not_8_out, E);
  and and_1 (and_1_out, not_1_out, not_2_out, 1'b1, not_3_out, I0);
  and and_2 (and_2_out, not_4_out, S0, 1'b1, not_5_out, I1);
  and and_3 (and_3_out, S1, not_6_out, 1'b1, not_7_out, I2);
  and and_4 (and_4_out, S1, S0, 1'b1, not_8_out, I3);
  or or_1 (Y, and_1_out, and_2_out, 1'b0, and_3_out, and_4_out);
endmodule

module _74154 (
  input  E1,
  input  E0,
  input  A3,
  input  A2,
  input  A1,
  input  A0,
  output Y15,
  output Y14,
  output Y13,
  output Y12,
  output Y11,
  output Y10,
  output Y9,
  output Y8,
  output Y7,
  output Y6,
  output Y5,
  output Y4,
  output Y3,
  output Y2,
  output Y1,
  output Y0
);

  wire not_1_out, not_2_out, not_3_out, not_4_out, not_5_out, not_6_out, not_7_out, not_8_out, not_9_out,
       not_10_out, not_11_out, not_12_out, not_13_out, not_14_out, not_15_out, not_16_out, not_17_out,
       not_18_out, not_19_out, not_20_out, not_21_out, not_22_out, not_23_out, not_24_out, not_25_out,
       not_26_out, not_27_out, not_28_out, not_29_out, not_30_out, not_31_out, not_32_out, not_33_out,
       not_34_out, not_35_out, not_36_out, not_37_out, not_38_out, not_39_out, not_40_out, not_41_out,
       not_42_out, not_43_out, not_44_out, not_45_out, not_46_out, not_47_out, not_48_out, not_49_out,
       not_50_out, not_51_out, not_52_out, not_53_out, not_54_out, not_55_out, not_56_out, not_57_out,
       not_58_out, not_59_out, not_60_out, not_61_out, not_62_out, not_63_out, not_64_out;

  not not_1 (not_1_out, E1);
  not not_2 (not_2_out, E0);
  not not_3 (not_3_out, E1);
  not not_4 (not_4_out, E0);
  not not_5 (not_5_out, A0);
  not not_6 (not_6_out, E1);
  not not_7 (not_7_out, E0);
  not not_8 (not_8_out, A1);
  not not_9 (not_9_out, E1);
  not not_10 (not_10_out, E0);
  not not_11 (not_11_out, A1);
  not not_12 (not_12_out, A0);
  not not_13 (not_13_out, E1);
  not not_14 (not_14_out, E0);
  not not_15 (not_15_out, A2);
  not not_16 (not_16_out, E1);
  not not_17 (not_17_out, E0);
  not not_18 (not_18_out, A2);
  not not_19 (not_19_out, A0);
  not not_20 (not_20_out, E1);
  not not_21 (not_21_out, E0);
  not not_22 (not_22_out, A2);
  not not_23 (not_23_out, A1);
  not not_24 (not_24_out, E1);
  not not_25 (not_25_out, E0);
  not not_26 (not_26_out, A2);
  not not_27 (not_27_out, A1);
  not not_28 (not_28_out, A0);
  not not_29 (not_29_out, E1);
  not not_30 (not_30_out, E0);
  not not_31 (not_31_out, A3);
  not not_32 (not_32_out, E1);
  not not_33 (not_33_out, E0);
  not not_34 (not_34_out, A3);
  not not_35 (not_35_out, A0);
  not not_36 (not_36_out, E1);
  not not_37 (not_37_out, E0);
  not not_38 (not_38_out, A3);
  not not_39 (not_39_out, A1);
  not not_40 (not_40_out, E1);
  not not_41 (not_41_out, E0);
  not not_42 (not_42_out, A3);
  not not_43 (not_43_out, A1);
  not not_44 (not_44_out, A0);
  not not_45 (not_45_out, E1);
  not not_46 (not_46_out, E0);
  not not_47 (not_47_out, A3);
  not not_48 (not_48_out, A2);
  not not_49 (not_49_out, E1);
  not not_50 (not_50_out, E0);
  not not_51 (not_51_out, A3);
  not not_52 (not_52_out, A2);
  not not_53 (not_53_out, A0);
  not not_54 (not_54_out, E1);
  not not_55 (not_55_out, E0);
  not not_56 (not_56_out, A3);
  not not_57 (not_57_out, A2);
  not not_58 (not_58_out, A1);
  not not_59 (not_59_out, E1);
  not not_60 (not_60_out, E0);
  not not_61 (not_61_out, A3);
  not not_62 (not_62_out, A2);
  not not_63 (not_63_out, A1);
  not not_64 (not_64_out, A0);
  nand nand_1 (Y15, not_1_out, not_2_out, A3, 1'b1, A2, A1, A0);
  // NOT_Gate not_65 has open pins: in=A3, out=open
  nand nand_2 (Y14, not_3_out, not_4_out, A3, 1'b1, A2, A1, not_5_out);
  nand nand_3 (Y13, not_6_out, not_7_out, A3, 1'b1, A2, not_8_out, A0);
  nand nand_4 (Y12, not_9_out, not_10_out, A3, 1'b1, A2, not_11_out, not_12_out);
  nand nand_5 (Y11, not_13_out, not_14_out, A3, 1'b1, not_15_out, A1, A0);
  nand nand_6 (Y10, not_16_out, not_17_out, A3, 1'b1, not_18_out, A1, not_19_out);
  nand nand_7 (Y9, not_20_out, not_21_out, A3, 1'b1, not_22_out, not_23_out, A0);
  nand nand_8 (Y8, not_24_out, not_25_out, A3, 1'b1, not_26_out, not_27_out, not_28_out);
  nand nand_9 (Y7, not_29_out, not_30_out, not_31_out, 1'b1, A2, A1, A0);
  nand nand_10 (Y6, not_32_out, not_33_out, not_34_out, 1'b1, A2, A1, not_35_out);
  nand nand_11 (Y5, not_36_out, not_37_out, not_38_out, 1'b1, A2, not_39_out, A0);
  nand nand_12 (Y4, not_40_out, not_41_out, not_42_out, 1'b1, A2, not_43_out, not_44_out);
  nand nand_13 (Y3, not_45_out, not_46_out, not_47_out, 1'b1, not_48_out, A1, A0);
  nand nand_14 (Y2, not_49_out, not_50_out, not_51_out, 1'b1, not_52_out, A1, not_53_out);
  nand nand_15 (Y1, not_54_out, not_55_out, not_56_out, 1'b1, not_57_out, not_58_out, A0);
  nand nand_16 (Y0, not_59_out, not_60_out, not_61_out, 1'b1, not_62_out, not_63_out, not_64_out);
endmodule

module _74157 (
  input  B3,
  input  B2,
  input  B1,
  input  B0,
  input  A3,
  input  A2,
  input  A1,
  input  A0,
  input  S,
  input  E,
  output Y3,
  output Y2,
  output Y1,
  output Y0
);

  wire and_1_out, and_2_out, and_3_out, and_4_out, and_5_out, and_6_out, and_7_out, and_8_out, not_1_out,
       not_2_out;

  not not_1 (not_1_out, S);
  not not_2 (not_2_out, E);
  and and_1 (and_1_out, B3, S, not_2_out);
  and and_2 (and_2_out, A3, not_1_out, not_2_out);
  and and_3 (and_3_out, B2, S, not_2_out);
  and and_4 (and_4_out, A2, not_1_out, not_2_out);
  and and_5 (and_5_out, B1, S, not_2_out);
  and and_6 (and_6_out, A1, not_1_out, not_2_out);
  and and_7 (and_7_out, B0, S, not_2_out);
  and and_8 (and_8_out, A0, not_1_out, not_2_out);
  or or_1 (Y3, and_1_out, and_2_out);
  or or_2 (Y2, and_3_out, and_4_out);
  or or_3 (Y1, and_5_out, and_6_out);
  or or_4 (Y0, and_7_out, and_8_out);
endmodule

module _74181 (
  input  S3,
  input  S2,
  input  S1,
  input  S0,
  input  B3,
  input  B2,
  input  B1,
  input  B0,
  input  A3,
  input  A2,
  input  A1,
  input  A0,
  input  M,
  input  C0,
  output G,
  output C4,
  output P,
  output A_B,
  output F3,
  output F2,
  output F1,
  output F0
);

  wire and_1_out, and_2_out, and_3_out, and_4_out, and_5_out, and_6_out, and_7_out, and_8_out, and_9_out,
       and_10_out, and_11_out, and_12_out, and_13_out, and_14_out, and_15_out, and_16_out, and_17_out,
       and_18_out, and_19_out, and_20_out, and_21_out, and_22_out, and_23_out, and_24_out, and_25_out,
       and_26_out, and_27_out, and_28_out, and_29_out, and_30_out, and_31_out, and_32_out, buffer_1_out,
       buffer_2_out, buffer_3_out, buffer_4_out, buffer_5_out, nand_1_out, nand_3_out, nor_1_out, nor_2_out,
       nor_3_out, nor_4_out, nor_5_out, nor_6_out, nor_7_out, nor_8_out, nor_10_out, nor_11_out, nor_12_out,
       not_1_out, not_2_out, not_3_out, not_4_out, not_5_out, not_6_out, not_7_out, not_8_out, not_9_out,
       not_10_out, not_11_out;

  not not_1 (not_1_out, B3);
  not not_2 (not_2_out, B2);
  not not_3 (not_3_out, B1);
  not not_4 (not_4_out, B0);
  and and_1 (and_1_out, S3, B3, A3);
  nor nor_1 (nor_1_out, and_1_out, and_2_out);
  and and_2 (and_2_out, A3, S2, not_1_out);
  and and_3 (and_3_out, not_1_out, S1);
  and and_4 (and_4_out, S0, B3);
  nor nor_2 (nor_2_out, and_3_out, and_4_out, buffer_1_out);
  buf buffer_1 (buffer_1_out, A3);
  and and_5 (and_5_out, S3, B2, A2);
  nor nor_3 (nor_3_out, and_5_out, and_6_out);
  and and_6 (and_6_out, A2, S2, not_2_out);
  and and_7 (and_7_out, not_2_out, S1);
  and and_8 (and_8_out, S0, B2);
  nor nor_4 (nor_4_out, and_7_out, and_8_out, buffer_2_out);
  buf buffer_2 (buffer_2_out, A2);
  and and_9 (and_9_out, S3, B1, A1);
  nor nor_5 (nor_5_out, and_9_out, and_10_out);
  and and_10 (and_10_out, A1, S2, not_3_out);
  and and_11 (and_11_out, not_3_out, S1);
  nor nor_6 (nor_6_out, and_11_out, and_12_out, buffer_3_out);
  and and_12 (and_12_out, S0, B1);
  buf buffer_3 (buffer_3_out, A1);
  and and_13 (and_13_out, S3, B0, A0);
  nor nor_7 (nor_7_out, and_13_out, and_14_out);
  and and_14 (and_14_out, A0, S2, not_4_out);
  and and_15 (and_15_out, not_4_out, S1);
  and and_16 (and_16_out, S0, B0);
  nor nor_8 (nor_8_out, and_15_out, and_16_out, buffer_4_out);
  buf buffer_4 (buffer_4_out, A0);
  not not_5 (not_5_out, M);
  buf buffer_5 (buffer_5_out, nor_2_out);
  and and_17 (and_17_out, nor_1_out, nor_4_out);
  and and_18 (and_18_out, nor_1_out, nor_3_out, nor_6_out);
  and and_19 (and_19_out, nor_1_out, nor_3_out, nor_5_out, nor_8_out, 1'b1);
  nand nand_1 (nand_1_out, nor_1_out, nor_3_out, nor_5_out, nor_7_out, C0);
  nand nand_2 (P, nor_1_out, nor_3_out, nor_5_out, nor_7_out, 1'b1);
  not not_6 (not_6_out, nor_2_out);
  and and_20 (and_20_out, nor_3_out, nor_5_out, nor_7_out, C0, not_5_out);
  and and_21 (and_21_out, nor_3_out, nor_5_out, nor_8_out, not_5_out, 1'b1);
  and and_22 (and_22_out, nor_3_out, nor_6_out, not_5_out);
  and and_23 (and_23_out, nor_4_out, not_5_out);
  not not_7 (not_7_out, nor_4_out);
  and and_24 (and_24_out, nor_5_out, nor_7_out, C0, not_5_out, 1'b1);
  and and_25 (and_25_out, nor_5_out, nor_8_out, not_5_out);
  and and_26 (and_26_out, nor_6_out, not_5_out);
  not not_8 (not_8_out, nor_6_out);
  and and_27 (and_27_out, C0, nor_7_out, not_5_out);
  and and_28 (and_28_out, nor_8_out, not_5_out);
  not not_9 (not_9_out, nor_8_out);
  nand nand_3 (nand_3_out, not_5_out, C0);
  nor nor_9 (G, buffer_5_out, and_17_out, and_18_out, and_19_out, 1'b0);
  and and_29 (and_29_out, nor_1_out, not_6_out);
  nor nor_10 (nor_10_out, and_20_out, and_21_out, and_22_out, and_23_out, 1'b0);
  and and_30 (and_30_out, nor_3_out, not_7_out);
  nor nor_11 (nor_11_out, and_24_out, and_25_out, and_26_out);
  and and_31 (and_31_out, nor_5_out, not_8_out);
  nor nor_12 (nor_12_out, and_27_out, and_28_out);
  and and_32 (and_32_out, nor_7_out, not_9_out);
  not not_10 (not_10_out, G);
  or or_1 (C4, not_10_out, not_11_out);
  not not_11 (not_11_out, nand_1_out);
  xor xor_1 (F3, and_29_out, nor_10_out);
  xor xor_2 (F2, and_30_out, nor_11_out);
  xor xor_3 (F1, and_31_out, nor_12_out);
  xor xor_4 (F0, and_32_out, nand_3_out);
  and and_33 (A_B, F3, F2, F1, F0, 1'b1);
endmodule

module _74238 (
  input  E2,
  input  E1,
  input  E0,
  input  A2,
  input  A1,
  input  A0,
  output Y7,
  output Y6,
  output Y5,
  output Y4,
  output Y3,
  output Y2,
  output Y1,
  output Y0
);

  wire not_1_out, not_2_out, not_3_out, not_4_out, not_5_out, not_6_out, not_7_out, not_8_out, not_9_out,
       not_10_out, not_11_out, not_12_out, not_13_out, not_14_out, not_15_out, not_16_out, not_17_out,
       not_18_out, not_19_out, not_20_out, not_21_out, not_22_out, not_23_out, not_24_out, not_25_out,
       not_26_out, not_27_out, not_28_out;

  not not_1 (not_1_out, E1);
  not not_2 (not_2_out, E0);
  not not_3 (not_3_out, E1);
  not not_4 (not_4_out, E0);
  not not_5 (not_5_out, A0);
  not not_6 (not_6_out, E1);
  not not_7 (not_7_out, E0);
  not not_8 (not_8_out, A1);
  not not_9 (not_9_out, E1);
  not not_10 (not_10_out, E0);
  not not_11 (not_11_out, A1);
  not not_12 (not_12_out, A0);
  not not_13 (not_13_out, E1);
  not not_14 (not_14_out, E0);
  not not_15 (not_15_out, A2);
  not not_16 (not_16_out, E1);
  not not_17 (not_17_out, E0);
  not not_18 (not_18_out, A2);
  not not_19 (not_19_out, A0);
  not not_20 (not_20_out, E1);
  not not_21 (not_21_out, E0);
  not not_22 (not_22_out, A2);
  not not_23 (not_23_out, A1);
  not not_24 (not_24_out, E1);
  not not_25 (not_25_out, E0);
  not not_26 (not_26_out, A2);
  not not_27 (not_27_out, A1);
  not not_28 (not_28_out, A0);
  and and_1 (Y7, E2, not_1_out, not_2_out, 1'b1, A2, A1, A0);
  and and_2 (Y6, E2, not_3_out, not_4_out, 1'b1, A2, A1, not_5_out);
  and and_3 (Y5, E2, not_6_out, not_7_out, 1'b1, A2, not_8_out, A0);
  and and_4 (Y4, E2, not_9_out, not_10_out, 1'b1, A2, not_11_out, not_12_out);
  and and_5 (Y3, E2, not_13_out, not_14_out, 1'b1, not_15_out, A1, A0);
  and and_6 (Y2, E2, not_16_out, not_17_out, 1'b1, not_18_out, A1, not_19_out);
  and and_7 (Y1, E2, not_20_out, not_21_out, 1'b1, not_22_out, not_23_out, A0);
  and and_8 (Y0, E2, not_24_out, not_25_out, 1'b1, not_26_out, not_27_out, not_28_out);
endmodule

module _74381 (
  input  B3,
  input  B2,
  input  B1,
  input  B0,
  input  A3,
  input  A2,
  input  A1,
  input  A0,
  input  S2,
  input  S1,
  input  S0,
  input  Cn,
  output F3,
  output F2,
  output F1,
  output F0,
  output P,
  output G
);

  wire and_1_out, and_2_out, and_3_out, and_4_out, and_5_out, and_6_out, and_7_out, and_8_out, and_9_out,
       and_10_out, and_11_out, and_12_out, and_13_out, and_14_out, and_15_out, and_16_out, and_17_out,
       and_18_out, and_19_out, and_20_out, and_21_out, and_22_out, and_23_out, and_24_out, and_25_out,
       and_26_out, and_27_out, and_28_out, and_29_out, and_30_out, and_31_out, and_32_out, and_33_out,
       and_34_out, and_35_out, and_36_out, and_37_out, and_38_out, and_39_out, and_40_out, and_41_out,
       and_42_out, and_43_out, and_44_out, nand_1_out, nand_2_out, nand_3_out, nand_4_out, nand_5_out,
       nor_1_out, nor_2_out, nor_3_out, nor_4_out, nor_5_out, nor_6_out, nor_7_out, nor_8_out, nor_9_out,
       nor_10_out, nor_11_out, nor_12_out, not_1_out, not_2_out, not_3_out, not_4_out, not_5_out, not_6_out,
       not_7_out, not_8_out, not_9_out, not_10_out, not_11_out, not_12_out, not_13_out, not_14_out;

  not not_1 (not_1_out, S0);
  not not_2 (not_2_out, not_1_out);
  not not_3 (not_3_out, S1);
  not not_4 (not_4_out, not_3_out);
  not not_5 (not_5_out, S2);
  not not_6 (not_6_out, not_5_out);
  not not_7 (not_7_out, B0);
  not not_8 (not_8_out, A0);
  not not_9 (not_9_out, B1);
  not not_10 (not_10_out, A1);
  not not_11 (not_11_out, B2);
  not not_12 (not_12_out, A2);
  not not_13 (not_13_out, B3);
  not not_14 (not_14_out, A3);
  nand nand_1 (nand_1_out, not_1_out, not_3_out);
  nand nand_2 (nand_2_out, not_3_out, not_5_out);
  and and_1 (and_1_out, not_1_out, not_6_out);
  nand nand_3 (nand_3_out, not_1_out, not_4_out);
  and and_2 (and_2_out, not_3_out, not_6_out);
  nand nand_4 (nand_4_out, not_2_out, not_4_out, not_5_out);
  nor nor_1 (nor_1_out, and_1_out, and_2_out);
  and and_3 (and_3_out, not_8_out, not_7_out, nand_3_out, nand_2_out, 1'b1);
  and and_4 (and_4_out, nand_1_out, nand_3_out, nand_4_out, not_7_out, A0);
  and and_5 (and_5_out, nand_2_out, nand_4_out, B0, not_8_out, 1'b1);
  and and_6 (and_6_out, not_8_out, not_7_out, nand_1_out, nand_4_out, nor_1_out);
  and and_7 (and_7_out, nand_2_out, nand_3_out, not_7_out, A0, 1'b1);
  and and_8 (and_8_out, nand_2_out, nand_3_out, B0, not_8_out, 1'b1);
  and and_9 (and_9_out, nand_1_out, nand_4_out, B0, A0, 1'b1);
  and and_10 (and_10_out, not_10_out, not_9_out, nand_3_out, nand_2_out, 1'b1);
  and and_11 (and_11_out, nand_1_out, nand_3_out, nand_4_out, not_9_out, A1);
  and and_12 (and_12_out, nand_2_out, nand_4_out, B1, not_10_out, 1'b1);
  and and_13 (and_13_out, not_10_out, not_9_out, nand_1_out, nand_4_out, nor_1_out);
  and and_14 (and_14_out, nand_2_out, nand_3_out, not_9_out, A1, 1'b1);
  and and_15 (and_15_out, nand_2_out, nand_3_out, B1, not_10_out, 1'b1);
  and and_16 (and_16_out, nand_1_out, nand_4_out, B1, A1, 1'b1);
  and and_17 (and_17_out, not_12_out, not_11_out, nand_3_out, nand_2_out, 1'b1);
  and and_18 (and_18_out, nand_1_out, nand_3_out, nand_4_out, not_11_out, A2);
  and and_19 (and_19_out, nand_2_out, nand_4_out, B2, not_12_out, 1'b1);
  and and_20 (and_20_out, not_12_out, not_11_out, nand_1_out, nand_4_out, nor_1_out);
  and and_21 (and_21_out, nand_2_out, nand_3_out, not_11_out, A2, 1'b1);
  and and_22 (and_22_out, nand_2_out, nand_3_out, B2, not_12_out, 1'b1);
  and and_23 (and_23_out, nand_1_out, nand_4_out, B2, A2, 1'b1);
  and and_24 (and_24_out, not_14_out, not_13_out, nand_3_out, nand_2_out, 1'b1);
  and and_25 (and_25_out, nand_1_out, nand_3_out, nand_4_out, not_13_out, A3);
  and and_26 (and_26_out, nand_2_out, nand_4_out, B3, not_14_out, 1'b1);
  and and_27 (and_27_out, not_14_out, not_13_out, nand_1_out, nand_4_out, nor_1_out);
  and and_28 (and_28_out, nand_2_out, nand_3_out, not_13_out, A3, 1'b1);
  and and_29 (and_29_out, nand_2_out, nand_3_out, B3, not_14_out, 1'b1);
  and and_30 (and_30_out, nand_1_out, nand_4_out, B3, A3, 1'b1);
  and and_31 (and_31_out, nand_1_out, not_5_out);
  nor nor_2 (nor_2_out, and_3_out, and_4_out, and_5_out);
  nor nor_3 (nor_3_out, and_6_out, and_7_out, and_8_out, and_9_out, 1'b0);
  nor nor_4 (nor_4_out, and_10_out, and_11_out, and_12_out);
  nor nor_5 (nor_5_out, and_13_out, and_14_out, and_15_out, and_16_out, 1'b0);
  nor nor_6 (nor_6_out, and_17_out, and_18_out, and_19_out);
  nor nor_7 (nor_7_out, and_20_out, and_21_out, and_22_out, and_23_out, 1'b0);
  nor nor_8 (nor_8_out, and_24_out, and_25_out, and_26_out);
  nor nor_9 (nor_9_out, and_27_out, and_28_out, and_29_out, and_30_out, 1'b0);
  nand nand_5 (nand_5_out, Cn, and_31_out);
  and and_32 (and_32_out, Cn, nor_2_out, and_31_out);
  and and_33 (and_33_out, nor_2_out, nor_3_out, and_31_out);
  and and_34 (and_34_out, Cn, nor_2_out, nor_4_out, and_31_out, 1'b1);
  and and_35 (and_35_out, nor_2_out, nor_4_out, nor_3_out, and_31_out, 1'b1);
  and and_36 (and_36_out, nor_4_out, nor_5_out, and_31_out);
  and and_37 (and_37_out, Cn, nor_2_out, nor_4_out, nor_6_out, and_31_out);
  and and_38 (and_38_out, nor_2_out, nor_4_out, nor_6_out, nor_3_out, and_31_out);
  and and_39 (and_39_out, nor_4_out, nor_6_out, nor_3_out, and_31_out, 1'b1);
  and and_40 (and_40_out, nor_6_out, nor_7_out, and_31_out);
  nand nand_6 (P, nor_2_out, nor_4_out, nor_6_out, nor_8_out, 1'b1);
  and and_41 (and_41_out, nor_2_out, nor_4_out, nor_6_out, nor_8_out, nor_3_out);
  and and_42 (and_42_out, nor_4_out, nor_6_out, nor_8_out, nor_5_out, 1'b1);
  and and_43 (and_43_out, nor_6_out, nor_8_out, nor_7_out);
  and and_44 (and_44_out, nor_8_out, nor_9_out);
  xor xor_1 (F0, nand_5_out, nor_3_out);
  nor nor_10 (nor_10_out, and_32_out, and_33_out);
  nor nor_11 (nor_11_out, and_34_out, and_35_out, and_36_out);
  nor nor_12 (nor_12_out, and_37_out, and_38_out, and_39_out, and_40_out, 1'b0);
  nor nor_13 (G, and_41_out, and_42_out, and_43_out, and_44_out, 1'b0);
  xor xor_2 (F1, nor_10_out, nor_5_out);
  xor xor_3 (F2, nor_11_out, nor_7_out);
  xor xor_4 (F3, nor_12_out, nor_9_out);
endmodule

module pal4H1 (
  input  d,
  input  c,
  input  b,
  input  a,
  output F
);

  wire and_1_out, and_2_out, and_3_out, and_4_out, and_5_out, and_6_out, and_7_out, and_8_out, buffer_1_out,
       buffer_2_out, buffer_3_out, buffer_4_out, buffer_5_out, buffer_6_out, buffer_7_out, buffer_8_out,
       buffer_9_out, buffer_10_out, buffer_11_out, buffer_12_out, buffer_13_out, buffer_14_out,
       buffer_15_out, buffer_16_out, buffer_17_out, buffer_18_out, buffer_19_out, buffer_20_out,
       buffer_21_out, buffer_22_out, buffer_23_out, buffer_24_out, buffer_25_out, buffer_26_out,
       buffer_27_out, buffer_28_out, buffer_29_out, buffer_30_out, buffer_31_out, buffer_32_out,
       buffer_33_out, buffer_34_out, buffer_35_out, buffer_36_out, buffer_37_out, buffer_38_out,
       buffer_39_out, buffer_40_out, buffer_41_out, buffer_42_out, buffer_43_out, buffer_44_out,
       buffer_45_out, buffer_46_out, buffer_47_out, buffer_48_out, buffer_49_out, buffer_50_out,
       buffer_51_out, buffer_52_out, buffer_53_out, buffer_54_out, buffer_55_out, buffer_56_out,
       buffer_57_out, buffer_58_out, buffer_59_out, buffer_60_out, buffer_61_out, buffer_62_out,
       buffer_63_out, buffer_64_out, not_1_out, not_2_out, not_3_out, not_4_out;

  not not_1 (not_1_out, d);
  not not_2 (not_2_out, c);
  buf buffer_1 (buffer_1_out, d);
  buf buffer_2 (buffer_2_out, not_1_out);
  buf buffer_3 (buffer_3_out, d);
  buf buffer_4 (buffer_4_out, not_1_out);
  buf buffer_5 (buffer_5_out, d);
  buf buffer_6 (buffer_6_out, not_1_out);
  buf buffer_7 (buffer_7_out, d);
  buf buffer_8 (buffer_8_out, not_1_out);
  buf buffer_9 (buffer_9_out, d);
  buf buffer_10 (buffer_10_out, not_1_out);
  buf buffer_11 (buffer_11_out, d);
  buf buffer_12 (buffer_12_out, not_1_out);
  buf buffer_13 (buffer_13_out, d);
  buf buffer_14 (buffer_14_out, not_1_out);
  buf buffer_15 (buffer_15_out, d);
  buf buffer_16 (buffer_16_out, not_1_out);
  not not_3 (not_3_out, b);
  buf buffer_17 (buffer_17_out, c);
  buf buffer_18 (buffer_18_out, not_2_out);
  buf buffer_19 (buffer_19_out, b);
  buf buffer_20 (buffer_20_out, not_3_out);
  buf buffer_21 (buffer_21_out, c);
  buf buffer_22 (buffer_22_out, not_2_out);
  buf buffer_23 (buffer_23_out, b);
  buf buffer_24 (buffer_24_out, not_3_out);
  buf buffer_25 (buffer_25_out, c);
  buf buffer_26 (buffer_26_out, not_2_out);
  buf buffer_27 (buffer_27_out, b);
  buf buffer_28 (buffer_28_out, not_3_out);
  buf buffer_29 (buffer_29_out, c);
  buf buffer_30 (buffer_30_out, not_2_out);
  buf buffer_31 (buffer_31_out, b);
  buf buffer_32 (buffer_32_out, not_3_out);
  buf buffer_33 (buffer_33_out, c);
  buf buffer_34 (buffer_34_out, not_2_out);
  buf buffer_35 (buffer_35_out, b);
  buf buffer_36 (buffer_36_out, not_3_out);
  buf buffer_37 (buffer_37_out, c);
  buf buffer_38 (buffer_38_out, not_2_out);
  buf buffer_39 (buffer_39_out, b);
  buf buffer_40 (buffer_40_out, not_3_out);
  buf buffer_41 (buffer_41_out, c);
  buf buffer_42 (buffer_42_out, not_2_out);
  buf buffer_43 (buffer_43_out, b);
  buf buffer_44 (buffer_44_out, not_3_out);
  buf buffer_45 (buffer_45_out, c);
  buf buffer_46 (buffer_46_out, not_2_out);
  buf buffer_47 (buffer_47_out, b);
  buf buffer_48 (buffer_48_out, not_3_out);
  not not_4 (not_4_out, a);
  buf buffer_49 (buffer_49_out, a);
  buf buffer_50 (buffer_50_out, not_4_out);
  buf buffer_51 (buffer_51_out, a);
  buf buffer_52 (buffer_52_out, not_4_out);
  buf buffer_53 (buffer_53_out, a);
  buf buffer_54 (buffer_54_out, not_4_out);
  buf buffer_55 (buffer_55_out, a);
  buf buffer_56 (buffer_56_out, not_4_out);
  buf buffer_57 (buffer_57_out, a);
  buf buffer_58 (buffer_58_out, not_4_out);
  buf buffer_59 (buffer_59_out, a);
  buf buffer_60 (buffer_60_out, not_4_out);
  buf buffer_61 (buffer_61_out, a);
  buf buffer_62 (buffer_62_out, not_4_out);
  buf buffer_63 (buffer_63_out, a);
  buf buffer_64 (buffer_64_out, not_4_out);
  and and_1 (and_1_out, buffer_1_out, buffer_2_out, buffer_17_out, buffer_18_out, buffer_19_out, buffer_20_out, buffer_49_out, buffer_50_out, 1'b1);
  and and_2 (and_2_out, buffer_3_out, buffer_4_out, buffer_21_out, buffer_22_out, buffer_23_out, buffer_24_out, buffer_51_out, buffer_52_out, 1'b1);
  and and_3 (and_3_out, buffer_5_out, buffer_6_out, buffer_25_out, buffer_26_out, buffer_27_out, buffer_28_out, buffer_53_out, buffer_54_out, 1'b1);
  and and_4 (and_4_out, buffer_7_out, buffer_8_out, buffer_29_out, buffer_30_out, buffer_31_out, buffer_32_out, buffer_55_out, buffer_56_out, 1'b1);
  and and_5 (and_5_out, buffer_9_out, buffer_10_out, buffer_33_out, buffer_34_out, buffer_35_out, buffer_36_out, buffer_57_out, buffer_58_out, 1'b1);
  and and_6 (and_6_out, buffer_11_out, buffer_12_out, buffer_37_out, buffer_38_out, buffer_39_out, buffer_40_out, buffer_59_out, buffer_60_out, 1'b1);
  and and_7 (and_7_out, buffer_13_out, buffer_14_out, buffer_41_out, buffer_42_out, buffer_43_out, buffer_44_out, buffer_61_out, buffer_62_out, 1'b1);
  and and_8 (and_8_out, buffer_15_out, buffer_16_out, buffer_45_out, buffer_46_out, buffer_47_out, buffer_48_out, buffer_63_out, buffer_64_out, 1'b1);
  or or_1 (F, and_1_out, and_2_out, and_3_out, and_4_out, and_5_out, and_6_out, and_7_out, and_8_out, 1'b0);

  // Notes on the sheet:
  //   d: pull=up
endmodule

module sum_1b (
  input  B0,
  input  A0,
  input  Ci,
  output Co,
  output S
);

  wire and_1_out, and_2_out, and_3_out;

  and and_1 (and_1_out, B0, Ci);
  and and_2 (and_2_out, A0, B0);
  and and_3 (and_3_out, Ci, A0);
  xor xor_1 (S, B0, A0, Ci);
  or or_1 (Co, and_1_out, and_2_out, and_3_out);
endmodule
