// Logisim project cronograma3.circ as structural Verilog: 9 circuits, main circuit crono_1paso
module crono_1paso (
  input  ENTRADA,
  output [3:0] out_2,
  output [3:0] out_3,
  output [3:0] out_4,
  output [3:0] out_5,
  output SALIDA
);

  wire detector_0_seguido_de_1_1_salida, detector_1_seguido_de_0_1_salida, detector_2_0s_seguidos_1_salida,
       detector_2_1s_seguidos_1_salida, RELOJ_out;
  wire [1:0] priority_encoder_1_out;

  Clock RELOJ (.out(RELOJ_out));
  D_Flip_Flop d_ff_1 (.clk(RELOJ_out), .D(ENTRADA), .Q(SALIDA), .preset(1'b0), .en(1'b1), .reset(1'b0));  // open: Qn
  detector_2_0s_seguidos detector_2_0s_seguidos_1 (
    .RELOJ(RELOJ_out), .RESET(1'b0), .ENTRADA(ENTRADA), .SALIDA(detector_2_0s_seguidos_1_salida));
  detector_0_seguido_de_1 detector_0_seguido_de_1_1 (
    .RELOJ(RELOJ_out), .RESET(1'b0), .ENTRADA(ENTRADA), .SALIDA(detector_0_seguido_de_1_1_salida));
  detector_1_seguido_de_0 detector_1_seguido_de_0_1 (
    .RELOJ(RELOJ_out), .RESET(1'b0), .ENTRADA(ENTRADA), .SALIDA(detector_1_seguido_de_0_1_salida));
  detector_2_1s_seguidos detector_2_1s_seguidos_1 (
    .RELOJ(RELOJ_out), .RESET(1'b0), .ENTRADA(ENTRADA), .SALIDA(detector_2_1s_seguidos_1_salida));
  Priority_Encoder #(.select(2)) priority_encoder_1 (
    .in0(detector_2_0s_seguidos_1_salida), .in1(detector_0_seguido_de_1_1_salida),
    .in2(detector_1_seguido_de_0_1_salida), .in3(detector_2_1s_seguidos_1_salida),
    .out(priority_encoder_1_out), .en_in(1'b1));  // open: gs, en_out
  Multiplexer #(.select(2), .width(4)) multiplexer_1 (
    .in0(4'b0001), .in1(4'b1111), .in2(4'b1111), .in3(4'b1000), .out(out_2), .sel(priority_encoder_1_out));
  Multiplexer #(.select(2), .width(4)) multiplexer_2 (
    .in0(4'b0001), .in1(4'b1000), .in2(4'b0001), .in3(4'b1000), .out(out_3), .sel(priority_encoder_1_out));
  Multiplexer #(.select(2), .width(4)) multiplexer_3 (
    .in0(4'b0001), .in1(4'b1000), .in2(4'b0001), .in3(4'b1000), .out(out_4), .sel(priority_encoder_1_out));
  Multiplexer #(.select(2), .width(4)) multiplexer_4 (
    .in0(4'b0001), .in1(4'b1000), .in2(4'b0001), .in3(4'b1000), .out(out_5), .sel(priority_encoder_1_out));

  // Notes on the sheet:
  //   detectores
  //   dos 0s seguidos
  //   un 0 seguido de un 1
  //   un 1 seguido de un 0
  //   dos 1s seguidos
  //   datos para la matriz 4x4
  //   propagar estado
endmodule

module crono_33pasos (
  input  E,
  output [3:0] out_2,
  output [3:0] out_3,
  output [3:0] out_4,
  output [3:0] out_5,
  output [3:0] out_6,
  output [3:0] out_7,
  output [3:0] out_8,
  output [3:0] out_9,
  output [3:0] out_10,
  output [3:0] out_11,
  output [3:0] out_12,
  output [3:0] out_13,
  output [3:0] out_14,
  output [3:0] out_15,
  output [3:0] out_16,
  output [3:0] out_17,
  output [3:0] out_18,
  output [3:0] out_19,
  output [3:0] out_20,
  output [3:0] out_21,
  output [3:0] out_22,
  output [3:0] out_23,
  output [3:0] out_24,
  output [3:0] out_25,
  output [3:0] out_26,
  output [3:0] out_27,
  output [3:0] out_28,
  output [3:0] out_29,
  output [3:0] out_30,
  output [3:0] out_31,
  output [3:0] out_32,
  output [3:0] out_33,
  output [3:0] out_34,
  output [3:0] out_35,
  output [3:0] out_36,
  output [3:0] out_37,
  output [3:0] out_38,
  output [3:0] out_39,
  output [3:0] out_40,
  output [3:0] out_41,
  output [3:0] out_42,
  output [3:0] out_43,
  output [3:0] out_44,
  output [3:0] out_45,
  output [3:0] out_46,
  output [3:0] out_47,
  output [3:0] out_48,
  output [3:0] out_49,
  output [3:0] out_50,
  output [3:0] out_51,
  output [3:0] out_52,
  output [3:0] out_53,
  output [3:0] out_54,
  output [3:0] out_55,
  output [3:0] out_56,
  output [3:0] out_57,
  output [3:0] out_58,
  output [3:0] out_59,
  output [3:0] out_60,
  output [3:0] out_61,
  output [3:0] out_62,
  output [3:0] out_63,
  output [3:0] out_64,
  output [3:0] out_65,
  output [3:0] out_66,
  output [3:0] out_67,
  output [3:0] out_68,
  output [3:0] out_69,
  output [3:0] out_70,
  output [3:0] out_71,
  output [3:0] out_72,
  output [3:0] out_73,
  output [3:0] out_74,
  output [3:0] out_75,
  output [3:0] out_76,
  output [3:0] out_77,
  output [3:0] out_78,
  output [3:0] out_79,
  output [3:0] out_80,
  output [3:0] out_81,
  output [3:0] out_82,
  output [3:0] out_83,
  output [3:0] out_84,
  output [3:0] out_85,
  output [3:0] out_86,
  output [3:0] out_87,
  output [3:0] out_88,
  output [3:0] out_89,
  output [3:0] out_90,
  output [3:0] out_91,
  output [3:0] out_92,
  output [3:0] out_93,
  output [3:0] out_94,
  output [3:0] out_95,
  output [3:0] out_96,
  output [3:0] out_97,
  output [3:0] out_98,
  output [3:0] out_99,
  output [3:0] out_100,
  output [3:0] out_101,
  output [3:0] out_102,
  output [3:0] out_103,
  output [3:0] out_104,
  output [3:0] out_105,
  output [3:0] out_106,
  output [3:0] out_107,
  output [3:0] out_108,
  output [3:0] out_109,
  output [3:0] out_110,
  output [3:0] out_111,
  output [3:0] out_112,
  output [3:0] out_113,
  output [3:0] out_114,
  output [3:0] out_115,
  output [3:0] out_116,
  output [3:0] out_117,
  output [3:0] out_118,
  output [3:0] out_119,
  output [3:0] out_120,
  output [3:0] out_121,
  output [3:0] out_122,
  output [3:0] out_123,
  output [3:0] out_124,
  output [3:0] out_125,
  output [3:0] out_126,
  output [3:0] out_127,
  output [3:0] out_128,
  output [3:0] out_129,
  output [3:0] out_130,
  output [3:0] out_131,
  output [3:0] out_132,
  output [3:0] out_133
);

  wire crono_1paso_2_salida, crono_1paso_3_salida, crono_1paso_4_salida, crono_1paso_5_salida,
       crono_1paso_6_salida, crono_1paso_7_salida, crono_1paso_8_salida, crono_1paso_9_salida,
       crono_1paso_10_salida, crono_1paso_11_salida, crono_1paso_12_salida, crono_1paso_13_salida,
       crono_1paso_14_salida, crono_1paso_15_salida, crono_1paso_16_salida, crono_1paso_17_salida,
       crono_1paso_18_salida, crono_1paso_19_salida, crono_1paso_20_salida, crono_1paso_21_salida,
       crono_1paso_22_salida, crono_1paso_23_salida, crono_1paso_24_salida, crono_1paso_25_salida,
       crono_1paso_26_salida, crono_1paso_27_salida, crono_1paso_28_salida, crono_1paso_29_salida,
       crono_1paso_30_salida, crono_1paso_31_salida, crono_1paso_32_salida, crono_1paso_33_salida;

  crono_1paso crono_1paso_1 (
    .ENTRADA(crono_1paso_2_salida), .out_2(out_2), .out_3(out_35), .out_4(out_68), .out_5(out_101));  // open: SALIDA
  crono_1paso crono_1paso_2 (
    .ENTRADA(crono_1paso_3_salida), .out_2(out_3), .out_3(out_36), .out_4(out_69), .out_5(out_102),
    .SALIDA(crono_1paso_2_salida));
  crono_1paso crono_1paso_3 (
    .ENTRADA(crono_1paso_4_salida), .out_2(out_4), .out_3(out_37), .out_4(out_70), .out_5(out_103),
    .SALIDA(crono_1paso_3_salida));
  crono_1paso crono_1paso_4 (
    .ENTRADA(crono_1paso_5_salida), .out_2(out_5), .out_3(out_38), .out_4(out_71), .out_5(out_104),
    .SALIDA(crono_1paso_4_salida));
  crono_1paso crono_1paso_5 (
    .ENTRADA(crono_1paso_6_salida), .out_2(out_6), .out_3(out_39), .out_4(out_72), .out_5(out_105),
    .SALIDA(crono_1paso_5_salida));
  crono_1paso crono_1paso_6 (
    .ENTRADA(crono_1paso_7_salida), .out_2(out_7), .out_3(out_40), .out_4(out_73), .out_5(out_106),
    .SALIDA(crono_1paso_6_salida));
  crono_1paso crono_1paso_7 (
    .ENTRADA(crono_1paso_8_salida), .out_2(out_8), .out_3(out_41), .out_4(out_74), .out_5(out_107),
    .SALIDA(crono_1paso_7_salida));
  crono_1paso crono_1paso_8 (
    .ENTRADA(crono_1paso_9_salida), .out_2(out_9), .out_3(out_42), .out_4(out_75), .out_5(out_108),
    .SALIDA(crono_1paso_8_salida));
  crono_1paso crono_1paso_9 (
    .ENTRADA(crono_1paso_10_salida), .out_2(out_10), .out_3(out_43), .out_4(out_76), .out_5(out_109),
    .SALIDA(crono_1paso_9_salida));
  crono_1paso crono_1paso_10 (
    .ENTRADA(crono_1paso_11_salida), .out_2(out_11), .out_3(out_44), .out_4(out_77), .out_5(out_110),
    .SALIDA(crono_1paso_10_salida));
  crono_1paso crono_1paso_11 (
    .ENTRADA(crono_1paso_12_salida), .out_2(out_12), .out_3(out_45), .out_4(out_78), .out_5(out_111),
    .SALIDA(crono_1paso_11_salida));
  crono_1paso crono_1paso_12 (
    .ENTRADA(crono_1paso_13_salida), .out_2(out_13), .out_3(out_46), .out_4(out_79), .out_5(out_112),
    .SALIDA(crono_1paso_12_salida));
  crono_1paso crono_1paso_13 (
    .ENTRADA(crono_1paso_14_salida), .out_2(out_14), .out_3(out_47), .out_4(out_80), .out_5(out_113),
    .SALIDA(crono_1paso_13_salida));
  crono_1paso crono_1paso_14 (
    .ENTRADA(crono_1paso_15_salida), .out_2(out_15), .out_3(out_48), .out_4(out_81), .out_5(out_114),
    .SALIDA(crono_1paso_14_salida));
  crono_1paso crono_1paso_15 (
    .ENTRADA(crono_1paso_16_salida), .out_2(out_16), .out_3(out_49), .out_4(out_82), .out_5(out_115),
    .SALIDA(crono_1paso_15_salida));
  crono_1paso crono_1paso_16 (
    .ENTRADA(crono_1paso_17_salida), .out_2(out_17), .out_3(out_50), .out_4(out_83), .out_5(out_116),
    .SALIDA(crono_1paso_16_salida));
  crono_1paso crono_1paso_17 (
    .ENTRADA(crono_1paso_18_salida), .out_2(out_18), .out_3(out_51), .out_4(out_84), .out_5(out_117),
    .SALIDA(crono_1paso_17_salida));
  crono_1paso crono_1paso_18 (
    .ENTRADA(crono_1paso_19_salida), .out_2(out_19), .out_3(out_52), .out_4(out_85), .out_5(out_118),
    .SALIDA(crono_1paso_18_salida));
  crono_1paso crono_1paso_19 (
    .ENTRADA(crono_1paso_20_salida), .out_2(out_20), .out_3(out_53), .out_4(out_86), .out_5(out_119),
    .SALIDA(crono_1paso_19_salida));
  crono_1paso crono_1paso_20 (
    .ENTRADA(crono_1paso_21_salida), .out_2(out_21), .out_3(out_54), .out_4(out_87), .out_5(out_120),
    .SALIDA(crono_1paso_20_salida));
  crono_1paso crono_1paso_21 (
    .ENTRADA(crono_1paso_22_salida), .out_2(out_22), .out_3(out_55), .out_4(out_88), .out_5(out_121),
    .SALIDA(crono_1paso_21_salida));
  crono_1paso crono_1paso_22 (
    .ENTRADA(crono_1paso_23_salida), .out_2(out_23), .out_3(out_56), .out_4(out_89), .out_5(out_122),
    .SALIDA(crono_1paso_22_salida));
  crono_1paso crono_1paso_23 (
    .ENTRADA(crono_1paso_24_salida), .out_2(out_24), .out_3(out_57), .out_4(out_90), .out_5(out_123),
    .SALIDA(crono_1paso_23_salida));
  crono_1paso crono_1paso_24 (
    .ENTRADA(crono_1paso_25_salida), .out_2(out_25), .out_3(out_58), .out_4(out_91), .out_5(out_124),
    .SALIDA(crono_1paso_24_salida));
  crono_1paso crono_1paso_25 (
    .ENTRADA(crono_1paso_26_salida), .out_2(out_26), .out_3(out_59), .out_4(out_92), .out_5(out_125),
    .SALIDA(crono_1paso_25_salida));
  crono_1paso crono_1paso_26 (
    .ENTRADA(crono_1paso_27_salida), .out_2(out_27), .out_3(out_60), .out_4(out_93), .out_5(out_126),
    .SALIDA(crono_1paso_26_salida));
  crono_1paso crono_1paso_27 (
    .ENTRADA(crono_1paso_28_salida), .out_2(out_28), .out_3(out_61), .out_4(out_94), .out_5(out_127),
    .SALIDA(crono_1paso_27_salida));
  crono_1paso crono_1paso_28 (
    .ENTRADA(crono_1paso_29_salida), .out_2(out_29), .out_3(out_62), .out_4(out_95), .out_5(out_128),
    .SALIDA(crono_1paso_28_salida));
  crono_1paso crono_1paso_29 (
    .ENTRADA(crono_1paso_30_salida), .out_2(out_30), .out_3(out_63), .out_4(out_96), .out_5(out_129),
    .SALIDA(crono_1paso_29_salida));
  crono_1paso crono_1paso_30 (
    .ENTRADA(crono_1paso_31_salida), .out_2(out_31), .out_3(out_64), .out_4(out_97), .out_5(out_130),
    .SALIDA(crono_1paso_30_salida));
  crono_1paso crono_1paso_31 (
    .ENTRADA(crono_1paso_32_salida), .out_2(out_32), .out_3(out_65), .out_4(out_98), .out_5(out_131),
    .SALIDA(crono_1paso_31_salida));
  crono_1paso crono_1paso_32 (
    .ENTRADA(crono_1paso_33_salida), .out_2(out_33), .out_3(out_66), .out_4(out_99), .out_5(out_132),
    .SALIDA(crono_1paso_32_salida));
  crono_1paso crono_1paso_33 (
    .ENTRADA(E), .out_2(out_34), .out_3(out_67), .out_4(out_100), .out_5(out_133),
    .SALIDA(crono_1paso_33_salida));
endmodule

module detector_2_1s_seguidos (
  input  RELOJ,
  input  RESET,
  input  ENTRADA,
  output SALIDA
);

  wire and_1_out, and_2_out, j_k_ff_1_q, j_k_ff_2_qn, not_1_out;

  not not_1 (not_1_out, ENTRADA);
  and and_1 (and_1_out, ENTRADA, j_k_ff_1_q);
  and and_2 (and_2_out, j_k_ff_2_qn, ENTRADA);
  J_K_Flip_Flop j_k_ff_1 (
    .J(and_2_out), .clk(RELOJ), .K(1'b1), .Q(j_k_ff_1_q), .preset(RESET), .en(1'b1), .reset(RESET));  // open: Qn
  J_K_Flip_Flop j_k_ff_2 (
    .J(and_1_out), .clk(RELOJ), .K(not_1_out), .Q(SALIDA), .Qn(j_k_ff_2_qn), .preset(RESET), .en(1'b1),
    .reset(RESET));
endmodule

module detector_2_0s_seguidos (
  input  RELOJ,
  input  RESET,
  input  ENTRADA,
  output SALIDA
);

  wire and_1_out, and_2_out, j_k_ff_1_q, j_k_ff_2_qn, not_1_out;

  not not_1 (not_1_out, ENTRADA);
  and and_1 (and_1_out, j_k_ff_2_qn, not_1_out);
  and and_2 (and_2_out, j_k_ff_1_q, not_1_out);
  J_K_Flip_Flop j_k_ff_1 (
    .J(and_1_out), .clk(RELOJ), .K(1'b1), .Q(j_k_ff_1_q), .preset(RESET), .en(1'b1), .reset(RESET));  // open: Qn
  J_K_Flip_Flop j_k_ff_2 (
    .J(and_2_out), .clk(RELOJ), .K(ENTRADA), .Q(SALIDA), .Qn(j_k_ff_2_qn), .preset(RESET), .en(1'b1),
    .reset(RESET));
endmodule

module detector_0_seguido_de_1 (
  input  RELOJ,
  input  RESET,
  input  ENTRADA,
  output SALIDA
);

  wire and_1_out, j_k_ff_1_q, not_1_out;

  not not_1 (not_1_out, ENTRADA);
  and and_1 (and_1_out, ENTRADA, j_k_ff_1_q);
  J_K_Flip_Flop j_k_ff_1 (
    .J(not_1_out), .clk(RELOJ), .K(ENTRADA), .Q(j_k_ff_1_q), .preset(RESET), .en(1'b1), .reset(RESET));  // open: Qn
  J_K_Flip_Flop j_k_ff_2 (
    .J(and_1_out), .clk(RELOJ), .K(1'b1), .Q(SALIDA), .preset(RESET), .en(1'b1), .reset(RESET));  // open: Qn
endmodule

module detector_1_seguido_de_0 (
  input  RELOJ,
  input  RESET,
  input  ENTRADA,
  output SALIDA
);

  wire and_1_out, j_k_ff_1_q, not_1_out;

  not not_1 (not_1_out, ENTRADA);
  and and_1 (and_1_out, j_k_ff_1_q, not_1_out);
  J_K_Flip_Flop j_k_ff_1 (
    .J(ENTRADA), .clk(RELOJ), .K(not_1_out), .Q(j_k_ff_1_q), .preset(RESET), .en(1'b1), .reset(RESET));  // open: Qn
  J_K_Flip_Flop j_k_ff_2 (
    .J(and_1_out), .clk(RELOJ), .K(1'b1), .Q(SALIDA), .preset(RESET), .en(1'b1), .reset(RESET));  // open: Qn
endmodule

module patron (
  input  [4:0] N_ciclo,
  input  [31:0] E,
  output Patron
);

  wire multiplexer_1_out, multiplexer_2_out;

  Multiplexer #(.select(4)) multiplexer_1 (
    .in0(E[31]), .in1(E[30]), .in2(E[29]), .in3(E[28]), .in4(E[27]), .in5(E[26]), .in6(E[25]), .in7(E[24]),
    .in8(E[23]), .in9(E[22]), .in10(E[21]), .in11(E[20]), .in12(E[19]), .in13(E[18]), .in14(E[17]),
    .in15(E[16]), .out(multiplexer_1_out), .sel(N_ciclo[3:0]));
  Multiplexer #(.select(4)) multiplexer_2 (
    .in0(E[15]), .in1(E[14]), .in2(E[13]), .in3(E[12]), .in4(E[11]), .in5(E[10]), .in6(E[9]), .in7(E[8]),
    .in8(E[7]), .in9(E[6]), .in10(E[5]), .in11(E[4]), .in12(E[3]), .in13(E[2]), .in14(E[1]), .in15(E[0]),
    .out(multiplexer_2_out), .sel(N_ciclo[3:0]));
  Multiplexer multiplexer_3 (.in0(multiplexer_1_out), .in1(multiplexer_2_out), .out(Patron), .sel(N_ciclo[4]));
endmodule

module patron5 (
  input  reloj_in,
  input  [31:0] Patron1,
  input  [31:0] Patron2,
  input  [31:0] Patron3,
  input  [31:0] Patron4,
  input  [31:0] Patron5,
  output S1,
  output S2,
  output S3,
  output S4,
  output S5
);

  wire [4:0] counter_1_q;

  Counter #(.width(5), .max('h1f)) counter_1 (
    .load(1'b0), .count(1'b1), .Q(counter_1_q), .clk(reloj_in), .clr(1'b0));  // open: D, carry
  patron patron_1 (.N_ciclo(counter_1_q), .E(Patron1), .Patron(S1));
  patron patron_2 (.N_ciclo(counter_1_q), .E(Patron2), .Patron(S2));
  patron patron_3 (.N_ciclo(counter_1_q), .E(Patron3), .Patron(S3));
  patron patron_4 (.N_ciclo(counter_1_q), .E(Patron4), .Patron(S4));
  patron patron_5 (.N_ciclo(counter_1_q), .E(Patron5), .Patron(S5));
endmodule

module crono (
);

  wire detector_2_1s_seguidos_1_salida, patron5_1_s1, patron5_1_s2, reloj_out;
  wire [3:0] crono_33pasos_1_out_2, crono_33pasos_1_out_3, crono_33pasos_1_out_4, crono_33pasos_1_out_5,
       crono_33pasos_1_out_6, crono_33pasos_1_out_7, crono_33pasos_1_out_8, crono_33pasos_1_out_9,
       crono_33pasos_1_out_10, crono_33pasos_1_out_11, crono_33pasos_1_out_12, crono_33pasos_1_out_13,
       crono_33pasos_1_out_14, crono_33pasos_1_out_15, crono_33pasos_1_out_16, crono_33pasos_1_out_17,
       crono_33pasos_1_out_18, crono_33pasos_1_out_19, crono_33pasos_1_out_20, crono_33pasos_1_out_21,
       crono_33pasos_1_out_22, crono_33pasos_1_out_23, crono_33pasos_1_out_24, crono_33pasos_1_out_25,
       crono_33pasos_1_out_26, crono_33pasos_1_out_27, crono_33pasos_1_out_28, crono_33pasos_1_out_29,
       crono_33pasos_1_out_30, crono_33pasos_1_out_31, crono_33pasos_1_out_32, crono_33pasos_1_out_33,
       crono_33pasos_1_out_34, crono_33pasos_1_out_35, crono_33pasos_1_out_36, crono_33pasos_1_out_37,
       crono_33pasos_1_out_38, crono_33pasos_1_out_39, crono_33pasos_1_out_40, crono_33pasos_1_out_41,
       crono_33pasos_1_out_42, crono_33pasos_1_out_43, crono_33pasos_1_out_44, crono_33pasos_1_out_45,
       crono_33pasos_1_out_46, crono_33pasos_1_out_47, crono_33pasos_1_out_48, crono_33pasos_1_out_49,
       crono_33pasos_1_out_50, crono_33pasos_1_out_51, crono_33pasos_1_out_52, crono_33pasos_1_out_53,
       crono_33pasos_1_out_54, crono_33pasos_1_out_55, crono_33pasos_1_out_56, crono_33pasos_1_out_57,
       crono_33pasos_1_out_58, crono_33pasos_1_out_59, crono_33pasos_1_out_60, crono_33pasos_1_out_61,
       crono_33pasos_1_out_62, crono_33pasos_1_out_63, crono_33pasos_1_out_64, crono_33pasos_1_out_65,
       crono_33pasos_1_out_66, crono_33pasos_1_out_67, crono_33pasos_1_out_68, crono_33pasos_1_out_69,
       crono_33pasos_1_out_70, crono_33pasos_1_out_71, crono_33pasos_1_out_72, crono_33pasos_1_out_73,
       crono_33pasos_1_out_74, crono_33pasos_1_out_75, crono_33pasos_1_out_76, crono_33pasos_1_out_77,
       crono_33pasos_1_out_78, crono_33pasos_1_out_79, crono_33pasos_1_out_80, crono_33pasos_1_out_81,
       crono_33pasos_1_out_82, crono_33pasos_1_out_83, crono_33pasos_1_out_84, crono_33pasos_1_out_85,
       crono_33pasos_1_out_86, crono_33pasos_1_out_87, crono_33pasos_1_out_88, crono_33pasos_1_out_89,
       crono_33pasos_1_out_90, crono_33pasos_1_out_91, crono_33pasos_1_out_92, crono_33pasos_1_out_93,
       crono_33pasos_1_out_94, crono_33pasos_1_out_95, crono_33pasos_1_out_96, crono_33pasos_1_out_97,
       crono_33pasos_1_out_98, crono_33pasos_1_out_99, crono_33pasos_1_out_100, crono_33pasos_1_out_101,
       crono_33pasos_1_out_102, crono_33pasos_1_out_103, crono_33pasos_1_out_104, crono_33pasos_1_out_105,
       crono_33pasos_1_out_106, crono_33pasos_1_out_107, crono_33pasos_1_out_108, crono_33pasos_1_out_109,
       crono_33pasos_1_out_110, crono_33pasos_1_out_111, crono_33pasos_1_out_112, crono_33pasos_1_out_113,
       crono_33pasos_1_out_114, crono_33pasos_1_out_115, crono_33pasos_1_out_116, crono_33pasos_1_out_117,
       crono_33pasos_1_out_118, crono_33pasos_1_out_119, crono_33pasos_1_out_120, crono_33pasos_1_out_121,
       crono_33pasos_1_out_122, crono_33pasos_1_out_123, crono_33pasos_1_out_124, crono_33pasos_1_out_125,
       crono_33pasos_1_out_126, crono_33pasos_1_out_127, crono_33pasos_1_out_128, crono_33pasos_1_out_129,
       crono_33pasos_1_out_130, crono_33pasos_1_out_131, crono_33pasos_1_out_132, crono_33pasos_1_out_133,
       crono_33pasos_2_out_2, crono_33pasos_2_out_3, crono_33pasos_2_out_4, crono_33pasos_2_out_5,
       crono_33pasos_2_out_6, crono_33pasos_2_out_7, crono_33pasos_2_out_8, crono_33pasos_2_out_9,
       crono_33pasos_2_out_10, crono_33pasos_2_out_11, crono_33pasos_2_out_12, crono_33pasos_2_out_13,
       crono_33pasos_2_out_14, crono_33pasos_2_out_15, crono_33pasos_2_out_16, crono_33pasos_2_out_17,
       crono_33pasos_2_out_18, crono_33pasos_2_out_19, crono_33pasos_2_out_20, crono_33pasos_2_out_21,
       crono_33pasos_2_out_22, crono_33pasos_2_out_23, crono_33pasos_2_out_24, crono_33pasos_2_out_25,
       crono_33pasos_2_out_26, crono_33pasos_2_out_27, crono_33pasos_2_out_28, crono_33pasos_2_out_29,
       crono_33pasos_2_out_30, crono_33pasos_2_out_31, crono_33pasos_2_out_32, crono_33pasos_2_out_33,
       crono_33pasos_2_out_34, crono_33pasos_2_out_35, crono_33pasos_2_out_36, crono_33pasos_2_out_37,
       crono_33pasos_2_out_38, crono_33pasos_2_out_39, crono_33pasos_2_out_40, crono_33pasos_2_out_41,
       crono_33pasos_2_out_42, crono_33pasos_2_out_43, crono_33pasos_2_out_44, crono_33pasos_2_out_45,
       crono_33pasos_2_out_46, crono_33pasos_2_out_47, crono_33pasos_2_out_48, crono_33pasos_2_out_49,
       crono_33pasos_2_out_50, crono_33pasos_2_out_51, crono_33pasos_2_out_52, crono_33pasos_2_out_53,
       crono_33pasos_2_out_54, crono_33pasos_2_out_55, crono_33pasos_2_out_56, crono_33pasos_2_out_57,
       crono_33pasos_2_out_58, crono_33pasos_2_out_59, crono_33pasos_2_out_60, crono_33pasos_2_out_61,
       crono_33pasos_2_out_62, crono_33pasos_2_out_63, crono_33pasos_2_out_64, crono_33pasos_2_out_65,
       crono_33pasos_2_out_66, crono_33pasos_2_out_67, crono_33pasos_2_out_68, crono_33pasos_2_out_69,
       crono_33pasos_2_out_70, crono_33pasos_2_out_71, crono_33pasos_2_out_72, crono_33pasos_2_out_73,
       crono_33pasos_2_out_74, crono_33pasos_2_out_75, crono_33pasos_2_out_76, crono_33pasos_2_out_77,
       crono_33pasos_2_out_78, crono_33pasos_2_out_79, crono_33pasos_2_out_80, crono_33pasos_2_out_81,
       crono_33pasos_2_out_82, crono_33pasos_2_out_83, crono_33pasos_2_out_84, crono_33pasos_2_out_85,
       crono_33pasos_2_out_86, crono_33pasos_2_out_87, crono_33pasos_2_out_88, crono_33pasos_2_out_89,
       crono_33pasos_2_out_90, crono_33pasos_2_out_91, crono_33pasos_2_out_92, crono_33pasos_2_out_93,
       crono_33pasos_2_out_94, crono_33pasos_2_out_95, crono_33pasos_2_out_96, crono_33pasos_2_out_97,
       crono_33pasos_2_out_98, crono_33pasos_2_out_99, crono_33pasos_2_out_100, crono_33pasos_2_out_101,
       crono_33pasos_2_out_102, crono_33pasos_2_out_103, crono_33pasos_2_out_104, crono_33pasos_2_out_105,
       crono_33pasos_2_out_106, crono_33pasos_2_out_107, crono_33pasos_2_out_108, crono_33pasos_2_out_109,
       crono_33pasos_2_out_110, crono_33pasos_2_out_111, crono_33pasos_2_out_112, crono_33pasos_2_out_113,
       crono_33pasos_2_out_114, crono_33pasos_2_out_115, crono_33pasos_2_out_116, crono_33pasos_2_out_117,
       crono_33pasos_2_out_118, crono_33pasos_2_out_119, crono_33pasos_2_out_120, crono_33pasos_2_out_121,
       crono_33pasos_2_out_122, crono_33pasos_2_out_123, crono_33pasos_2_out_124, crono_33pasos_2_out_125,
       crono_33pasos_2_out_126, crono_33pasos_2_out_127, crono_33pasos_2_out_128, crono_33pasos_2_out_129,
       crono_33pasos_2_out_130, crono_33pasos_2_out_131, crono_33pasos_2_out_132, crono_33pasos_2_out_133,
       crono_33pasos_3_out_2, crono_33pasos_3_out_3, crono_33pasos_3_out_4, crono_33pasos_3_out_5,
       crono_33pasos_3_out_6, crono_33pasos_3_out_7, crono_33pasos_3_out_8, crono_33pasos_3_out_9,
       crono_33pasos_3_out_10, crono_33pasos_3_out_11, crono_33pasos_3_out_12, crono_33pasos_3_out_13,
       crono_33pasos_3_out_14, crono_33pasos_3_out_15, crono_33pasos_3_out_16, crono_33pasos_3_out_17,
       crono_33pasos_3_out_18, crono_33pasos_3_out_19, crono_33pasos_3_out_20, crono_33pasos_3_out_21,
       crono_33pasos_3_out_22, crono_33pasos_3_out_23, crono_33pasos_3_out_24, crono_33pasos_3_out_25,
       crono_33pasos_3_out_26, crono_33pasos_3_out_27, crono_33pasos_3_out_28, crono_33pasos_3_out_29,
       crono_33pasos_3_out_30, crono_33pasos_3_out_31, crono_33pasos_3_out_32, crono_33pasos_3_out_33,
       crono_33pasos_3_out_34, crono_33pasos_3_out_35, crono_33pasos_3_out_36, crono_33pasos_3_out_37,
       crono_33pasos_3_out_38, crono_33pasos_3_out_39, crono_33pasos_3_out_40, crono_33pasos_3_out_41,
       crono_33pasos_3_out_42, crono_33pasos_3_out_43, crono_33pasos_3_out_44, crono_33pasos_3_out_45,
       crono_33pasos_3_out_46, crono_33pasos_3_out_47, crono_33pasos_3_out_48, crono_33pasos_3_out_49,
       crono_33pasos_3_out_50, crono_33pasos_3_out_51, crono_33pasos_3_out_52, crono_33pasos_3_out_53,
       crono_33pasos_3_out_54, crono_33pasos_3_out_55, crono_33pasos_3_out_56, crono_33pasos_3_out_57,
       crono_33pasos_3_out_58, crono_33pasos_3_out_59, crono_33pasos_3_out_60, crono_33pasos_3_out_61,
       crono_33pasos_3_out_62, crono_33pasos_3_out_63, crono_33pasos_3_out_64, crono_33pasos_3_out_65,
       crono_33pasos_3_out_66, crono_33pasos_3_out_67, crono_33pasos_3_out_68, crono_33pasos_3_out_69,
       crono_33pasos_3_out_70, crono_33pasos_3_out_71, crono_33pasos_3_out_72, crono_33pasos_3_out_73,
       crono_33pasos_3_out_74, crono_33pasos_3_out_75, crono_33pasos_3_out_76, crono_33pasos_3_out_77,
       crono_33pasos_3_out_78, crono_33pasos_3_out_79, crono_33pasos_3_out_80, crono_33pasos_3_out_81,
       crono_33pasos_3_out_82, crono_33pasos_3_out_83, crono_33pasos_3_out_84, crono_33pasos_3_out_85,
       crono_33pasos_3_out_86, crono_33pasos_3_out_87, crono_33pasos_3_out_88, crono_33pasos_3_out_89,
       crono_33pasos_3_out_90, crono_33pasos_3_out_91, crono_33pasos_3_out_92, crono_33pasos_3_out_93,
       crono_33pasos_3_out_94, crono_33pasos_3_out_95, crono_33pasos_3_out_96, crono_33pasos_3_out_97,
       crono_33pasos_3_out_98, crono_33pasos_3_out_99, crono_33pasos_3_out_100, crono_33pasos_3_out_101,
       crono_33pasos_3_out_102, crono_33pasos_3_out_103, crono_33pasos_3_out_104, crono_33pasos_3_out_105,
       crono_33pasos_3_out_106, crono_33pasos_3_out_107, crono_33pasos_3_out_108, crono_33pasos_3_out_109,
       crono_33pasos_3_out_110, crono_33pasos_3_out_111, crono_33pasos_3_out_112, crono_33pasos_3_out_113,
       crono_33pasos_3_out_114, crono_33pasos_3_out_115, crono_33pasos_3_out_116, crono_33pasos_3_out_117,
       crono_33pasos_3_out_118, crono_33pasos_3_out_119, crono_33pasos_3_out_120, crono_33pasos_3_out_121,
       crono_33pasos_3_out_122, crono_33pasos_3_out_123, crono_33pasos_3_out_124, crono_33pasos_3_out_125,
       crono_33pasos_3_out_126, crono_33pasos_3_out_127, crono_33pasos_3_out_128, crono_33pasos_3_out_129,
       crono_33pasos_3_out_130, crono_33pasos_3_out_131, crono_33pasos_3_out_132, crono_33pasos_3_out_133;

  Clock reloj (.out(reloj_out));
  detector_2_1s_seguidos detector_2_1s_seguidos_1 (
    .RELOJ(reloj_out), .RESET(patron5_1_s1), .ENTRADA(patron5_1_s2), .SALIDA(detector_2_1s_seguidos_1_salida));
  patron5 patron5_1 (
    .reloj_in(reloj_out), .Patron1(32'h80000000), .Patron2(32'h7cdc5a9), .Patron3({32{1'b0}}),
    .Patron4({32{1'b0}}), .Patron5({32{1'b0}}), .S1(patron5_1_s1), .S2(patron5_1_s2));  // open: S3, S4, S5
  DotMatrix #(.matrixcols(4), .matrixrows(4)) dotmatrix_1 (
    .col0(crono_33pasos_1_out_2), .col1(crono_33pasos_1_out_35), .col2(crono_33pasos_1_out_68),
    .col3(crono_33pasos_1_out_101));
  crono_33pasos crono_33pasos_1 (
    .E(patron5_1_s1), .out_2(crono_33pasos_1_out_2), .out_35(crono_33pasos_1_out_35),
    .out_68(crono_33pasos_1_out_68), .out_101(crono_33pasos_1_out_101), .out_3(crono_33pasos_1_out_3),
    .out_36(crono_33pasos_1_out_36), .out_69(crono_33pasos_1_out_69), .out_102(crono_33pasos_1_out_102),
    .out_4(crono_33pasos_1_out_4), .out_37(crono_33pasos_1_out_37), .out_70(crono_33pasos_1_out_70),
    .out_103(crono_33pasos_1_out_103), .out_5(crono_33pasos_1_out_5), .out_38(crono_33pasos_1_out_38),
    .out_71(crono_33pasos_1_out_71), .out_104(crono_33pasos_1_out_104), .out_6(crono_33pasos_1_out_6),
    .out_39(crono_33pasos_1_out_39), .out_72(crono_33pasos_1_out_72), .out_105(crono_33pasos_1_out_105),
    .out_7(crono_33pasos_1_out_7), .out_40(crono_33pasos_1_out_40), .out_73(crono_33pasos_1_out_73),
    .out_106(crono_33pasos_1_out_106), .out_8(crono_33pasos_1_out_8), .out_41(crono_33pasos_1_out_41),
    .out_74(crono_33pasos_1_out_74), .out_107(crono_33pasos_1_out_107), .out_9(crono_33pasos_1_out_9),
    .out_42(crono_33pasos_1_out_42), .out_75(crono_33pasos_1_out_75), .out_108(crono_33pasos_1_out_108),
    .out_10(crono_33pasos_1_out_10), .out_43(crono_33pasos_1_out_43), .out_76(crono_33pasos_1_out_76),
    .out_109(crono_33pasos_1_out_109), .out_11(crono_33pasos_1_out_11), .out_44(crono_33pasos_1_out_44),
    .out_77(crono_33pasos_1_out_77), .out_110(crono_33pasos_1_out_110), .out_12(crono_33pasos_1_out_12),
    .out_45(crono_33pasos_1_out_45), .out_78(crono_33pasos_1_out_78), .out_111(crono_33pasos_1_out_111),
    .out_13(crono_33pasos_1_out_13), .out_46(crono_33pasos_1_out_46), .out_79(crono_33pasos_1_out_79),
    .out_112(crono_33pasos_1_out_112), .out_14(crono_33pasos_1_out_14), .out_47(crono_33pasos_1_out_47),
    .out_80(crono_33pasos_1_out_80), .out_113(crono_33pasos_1_out_113), .out_15(crono_33pasos_1_out_15),
    .out_48(crono_33pasos_1_out_48), .out_81(crono_33pasos_1_out_81), .out_114(crono_33pasos_1_out_114),
    .out_16(crono_33pasos_1_out_16), .out_49(crono_33pasos_1_out_49), .out_82(crono_33pasos_1_out_82),
    .out_115(crono_33pasos_1_out_115), .out_17(crono_33pasos_1_out_17), .out_50(crono_33pasos_1_out_50),
    .out_83(crono_33pasos_1_out_83), .out_116(crono_33pasos_1_out_116), .out_18(crono_33pasos_1_out_18),
    .out_51(crono_33pasos_1_out_51), .out_84(crono_33pasos_1_out_84), .out_117(crono_33pasos_1_out_117),
    .out_19(crono_33pasos_1_out_19), .out_52(crono_33pasos_1_out_52), .out_85(crono_33pasos_1_out_85),
    .out_118(crono_33pasos_1_out_118), .out_20(crono_33pasos_1_out_20), .out_53(crono_33pasos_1_out_53),
    .out_86(crono_33pasos_1_out_86), .out_119(crono_33pasos_1_out_119), .out_21(crono_33pasos_1_out_21),
    .out_54(crono_33pasos_1_out_54), .out_87(crono_33pasos_1_out_87), .out_120(crono_33pasos_1_out_120),
    .out_22(crono_33pasos_1_out_22), .out_55(crono_33pasos_1_out_55), .out_88(crono_33pasos_1_out_88),
    .out_121(crono_33pasos_1_out_121), .out_23(crono_33pasos_1_out_23), .out_56(crono_33pasos_1_out_56),
    .out_89(crono_33pasos_1_out_89), .out_122(crono_33pasos_1_out_122), .out_24(crono_33pasos_1_out_24),
    .out_57(crono_33pasos_1_out_57), .out_90(crono_33pasos_1_out_90), .out_123(crono_33pasos_1_out_123),
    .out_25(crono_33pasos_1_out_25), .out_58(crono_33pasos_1_out_58), .out_91(crono_33pasos_1_out_91),
    .out_124(crono_33pasos_1_out_124), .out_26(crono_33pasos_1_out_26), .out_59(crono_33pasos_1_out_59),
    .out_92(crono_33pasos_1_out_92), .out_125(crono_33pasos_1_out_125), .out_27(crono_33pasos_1_out_27),
    .out_60(crono_33pasos_1_out_60), .out_93(crono_33pasos_1_out_93), .out_126(crono_33pasos_1_out_126),
    .out_28(crono_33pasos_1_out_28), .out_61(crono_33pasos_1_out_61), .out_94(crono_33pasos_1_out_94),
    .out_127(crono_33pasos_1_out_127), .out_29(crono_33pasos_1_out_29), .out_62(crono_33pasos_1_out_62),
    .out_95(crono_33pasos_1_out_95), .out_128(crono_33pasos_1_out_128), .out_30(crono_33pasos_1_out_30),
    .out_63(crono_33pasos_1_out_63), .out_96(crono_33pasos_1_out_96), .out_129(crono_33pasos_1_out_129),
    .out_31(crono_33pasos_1_out_31), .out_64(crono_33pasos_1_out_64), .out_97(crono_33pasos_1_out_97),
    .out_130(crono_33pasos_1_out_130), .out_32(crono_33pasos_1_out_32), .out_65(crono_33pasos_1_out_65),
    .out_98(crono_33pasos_1_out_98), .out_131(crono_33pasos_1_out_131), .out_33(crono_33pasos_1_out_33),
    .out_66(crono_33pasos_1_out_66), .out_99(crono_33pasos_1_out_99), .out_132(crono_33pasos_1_out_132),
    .out_34(crono_33pasos_1_out_34), .out_67(crono_33pasos_1_out_67), .out_100(crono_33pasos_1_out_100),
    .out_133(crono_33pasos_1_out_133));
  DotMatrix #(.matrixcols(4), .matrixrows(4)) dotmatrix_2 (
    .col0(crono_33pasos_2_out_2), .col1(crono_33pasos_2_out_35), .col2(crono_33pasos_2_out_68),
    .col3(crono_33pasos_2_out_101));
  crono_33pasos crono_33pasos_2 (
    .E(patron5_1_s2), .out_2(crono_33pasos_2_out_2), .out_35(crono_33pasos_2_out_35),
    .out_68(crono_33pasos_2_out_68), .out_101(crono_33pasos_2_out_101), .out_3(crono_33pasos_2_out_3),
    .out_36(crono_33pasos_2_out_36), .out_69(crono_33pasos_2_out_69), .out_102(crono_33pasos_2_out_102),
    .out_4(crono_33pasos_2_out_4), .out_37(crono_33pasos_2_out_37), .out_70(crono_33pasos_2_out_70),
    .out_103(crono_33pasos_2_out_103), .out_5(crono_33pasos_2_out_5), .out_38(crono_33pasos_2_out_38),
    .out_71(crono_33pasos_2_out_71), .out_104(crono_33pasos_2_out_104), .out_6(crono_33pasos_2_out_6),
    .out_39(crono_33pasos_2_out_39), .out_72(crono_33pasos_2_out_72), .out_105(crono_33pasos_2_out_105),
    .out_7(crono_33pasos_2_out_7), .out_40(crono_33pasos_2_out_40), .out_73(crono_33pasos_2_out_73),
    .out_106(crono_33pasos_2_out_106), .out_8(crono_33pasos_2_out_8), .out_41(crono_33pasos_2_out_41),
    .out_74(crono_33pasos_2_out_74), .out_107(crono_33pasos_2_out_107), .out_9(crono_33pasos_2_out_9),
    .out_42(crono_33pasos_2_out_42), .out_75(crono_33pasos_2_out_75), .out_108(crono_33pasos_2_out_108),
    .out_10(crono_33pasos_2_out_10), .out_43(crono_33pasos_2_out_43), .out_76(crono_33pasos_2_out_76),
    .out_109(crono_33pasos_2_out_109), .out_11(crono_33pasos_2_out_11), .out_44(crono_33pasos_2_out_44),
    .out_77(crono_33pasos_2_out_77), .out_110(crono_33pasos_2_out_110), .out_12(crono_33pasos_2_out_12),
    .out_45(crono_33pasos_2_out_45), .out_78(crono_33pasos_2_out_78), .out_111(crono_33pasos_2_out_111),
    .out_13(crono_33pasos_2_out_13), .out_46(crono_33pasos_2_out_46), .out_79(crono_33pasos_2_out_79),
    .out_112(crono_33pasos_2_out_112), .out_14(crono_33pasos_2_out_14), .out_47(crono_33pasos_2_out_47),
    .out_80(crono_33pasos_2_out_80), .out_113(crono_33pasos_2_out_113), .out_15(crono_33pasos_2_out_15),
    .out_48(crono_33pasos_2_out_48), .out_81(crono_33pasos_2_out_81), .out_114(crono_33pasos_2_out_114),
    .out_16(crono_33pasos_2_out_16), .out_49(crono_33pasos_2_out_49), .out_82(crono_33pasos_2_out_82),
    .out_115(crono_33pasos_2_out_115), .out_17(crono_33pasos_2_out_17), .out_50(crono_33pasos_2_out_50),
    .out_83(crono_33pasos_2_out_83), .out_116(crono_33pasos_2_out_116), .out_18(crono_33pasos_2_out_18),
    .out_51(crono_33pasos_2_out_51), .out_84(crono_33pasos_2_out_84), .out_117(crono_33pasos_2_out_117),
    .out_19(crono_33pasos_2_out_19), .out_52(crono_33pasos_2_out_52), .out_85(crono_33pasos_2_out_85),
    .out_118(crono_33pasos_2_out_118), .out_20(crono_33pasos_2_out_20), .out_53(crono_33pasos_2_out_53),
    .out_86(crono_33pasos_2_out_86), .out_119(crono_33pasos_2_out_119), .out_21(crono_33pasos_2_out_21),
    .out_54(crono_33pasos_2_out_54), .out_87(crono_33pasos_2_out_87), .out_120(crono_33pasos_2_out_120),
    .out_22(crono_33pasos_2_out_22), .out_55(crono_33pasos_2_out_55), .out_88(crono_33pasos_2_out_88),
    .out_121(crono_33pasos_2_out_121), .out_23(crono_33pasos_2_out_23), .out_56(crono_33pasos_2_out_56),
    .out_89(crono_33pasos_2_out_89), .out_122(crono_33pasos_2_out_122), .out_24(crono_33pasos_2_out_24),
    .out_57(crono_33pasos_2_out_57), .out_90(crono_33pasos_2_out_90), .out_123(crono_33pasos_2_out_123),
    .out_25(crono_33pasos_2_out_25), .out_58(crono_33pasos_2_out_58), .out_91(crono_33pasos_2_out_91),
    .out_124(crono_33pasos_2_out_124), .out_26(crono_33pasos_2_out_26), .out_59(crono_33pasos_2_out_59),
    .out_92(crono_33pasos_2_out_92), .out_125(crono_33pasos_2_out_125), .out_27(crono_33pasos_2_out_27),
    .out_60(crono_33pasos_2_out_60), .out_93(crono_33pasos_2_out_93), .out_126(crono_33pasos_2_out_126),
    .out_28(crono_33pasos_2_out_28), .out_61(crono_33pasos_2_out_61), .out_94(crono_33pasos_2_out_94),
    .out_127(crono_33pasos_2_out_127), .out_29(crono_33pasos_2_out_29), .out_62(crono_33pasos_2_out_62),
    .out_95(crono_33pasos_2_out_95), .out_128(crono_33pasos_2_out_128), .out_30(crono_33pasos_2_out_30),
    .out_63(crono_33pasos_2_out_63), .out_96(crono_33pasos_2_out_96), .out_129(crono_33pasos_2_out_129),
    .out_31(crono_33pasos_2_out_31), .out_64(crono_33pasos_2_out_64), .out_97(crono_33pasos_2_out_97),
    .out_130(crono_33pasos_2_out_130), .out_32(crono_33pasos_2_out_32), .out_65(crono_33pasos_2_out_65),
    .out_98(crono_33pasos_2_out_98), .out_131(crono_33pasos_2_out_131), .out_33(crono_33pasos_2_out_33),
    .out_66(crono_33pasos_2_out_66), .out_99(crono_33pasos_2_out_99), .out_132(crono_33pasos_2_out_132),
    .out_34(crono_33pasos_2_out_34), .out_67(crono_33pasos_2_out_67), .out_100(crono_33pasos_2_out_100),
    .out_133(crono_33pasos_2_out_133));
  crono_33pasos crono_33pasos_3 (
    .E(detector_2_1s_seguidos_1_salida), .out_2(crono_33pasos_3_out_2), .out_35(crono_33pasos_3_out_35),
    .out_68(crono_33pasos_3_out_68), .out_101(crono_33pasos_3_out_101), .out_3(crono_33pasos_3_out_3),
    .out_36(crono_33pasos_3_out_36), .out_69(crono_33pasos_3_out_69), .out_102(crono_33pasos_3_out_102),
    .out_4(crono_33pasos_3_out_4), .out_37(crono_33pasos_3_out_37), .out_70(crono_33pasos_3_out_70),
    .out_103(crono_33pasos_3_out_103), .out_5(crono_33pasos_3_out_5), .out_38(crono_33pasos_3_out_38),
    .out_71(crono_33pasos_3_out_71), .out_104(crono_33pasos_3_out_104), .out_6(crono_33pasos_3_out_6),
    .out_39(crono_33pasos_3_out_39), .out_72(crono_33pasos_3_out_72), .out_105(crono_33pasos_3_out_105),
    .out_7(crono_33pasos_3_out_7), .out_40(crono_33pasos_3_out_40), .out_73(crono_33pasos_3_out_73),
    .out_106(crono_33pasos_3_out_106), .out_8(crono_33pasos_3_out_8), .out_41(crono_33pasos_3_out_41),
    .out_74(crono_33pasos_3_out_74), .out_107(crono_33pasos_3_out_107), .out_9(crono_33pasos_3_out_9),
    .out_42(crono_33pasos_3_out_42), .out_75(crono_33pasos_3_out_75), .out_108(crono_33pasos_3_out_108),
    .out_10(crono_33pasos_3_out_10), .out_43(crono_33pasos_3_out_43), .out_76(crono_33pasos_3_out_76),
    .out_109(crono_33pasos_3_out_109), .out_11(crono_33pasos_3_out_11), .out_44(crono_33pasos_3_out_44),
    .out_77(crono_33pasos_3_out_77), .out_110(crono_33pasos_3_out_110), .out_12(crono_33pasos_3_out_12),
    .out_45(crono_33pasos_3_out_45), .out_78(crono_33pasos_3_out_78), .out_111(crono_33pasos_3_out_111),
    .out_13(crono_33pasos_3_out_13), .out_46(crono_33pasos_3_out_46), .out_79(crono_33pasos_3_out_79),
    .out_112(crono_33pasos_3_out_112), .out_14(crono_33pasos_3_out_14), .out_47(crono_33pasos_3_out_47),
    .out_80(crono_33pasos_3_out_80), .out_113(crono_33pasos_3_out_113), .out_15(crono_33pasos_3_out_15),
    .out_48(crono_33pasos_3_out_48), .out_81(crono_33pasos_3_out_81), .out_114(crono_33pasos_3_out_114),
    .out_16(crono_33pasos_3_out_16), .out_49(crono_33pasos_3_out_49), .out_82(crono_33pasos_3_out_82),
    .out_115(crono_33pasos_3_out_115), .out_17(crono_33pasos_3_out_17), .out_50(crono_33pasos_3_out_50),
    .out_83(crono_33pasos_3_out_83), .out_116(crono_33pasos_3_out_116), .out_18(crono_33pasos_3_out_18),
    .out_51(crono_33pasos_3_out_51), .out_84(crono_33pasos_3_out_84), .out_117(crono_33pasos_3_out_117),
    .out_19(crono_33pasos_3_out_19), .out_52(crono_33pasos_3_out_52), .out_85(crono_33pasos_3_out_85),
    .out_118(crono_33pasos_3_out_118), .out_20(crono_33pasos_3_out_20), .out_53(crono_33pasos_3_out_53),
    .out_86(crono_33pasos_3_out_86), .out_119(crono_33pasos_3_out_119), .out_21(crono_33pasos_3_out_21),
    .out_54(crono_33pasos_3_out_54), .out_87(crono_33pasos_3_out_87), .out_120(crono_33pasos_3_out_120),
    .out_22(crono_33pasos_3_out_22), .out_55(crono_33pasos_3_out_55), .out_88(crono_33pasos_3_out_88),
    .out_121(crono_33pasos_3_out_121), .out_23(crono_33pasos_3_out_23), .out_56(crono_33pasos_3_out_56),
    .out_89(crono_33pasos_3_out_89), .out_122(crono_33pasos_3_out_122), .out_24(crono_33pasos_3_out_24),
    .out_57(crono_33pasos_3_out_57), .out_90(crono_33pasos_3_out_90), .out_123(crono_33pasos_3_out_123),
    .out_25(crono_33pasos_3_out_25), .out_58(crono_33pasos_3_out_58), .out_91(crono_33pasos_3_out_91),
    .out_124(crono_33pasos_3_out_124), .out_26(crono_33pasos_3_out_26), .out_59(crono_33pasos_3_out_59),
    .out_92(crono_33pasos_3_out_92), .out_125(crono_33pasos_3_out_125), .out_27(crono_33pasos_3_out_27),
    .out_60(crono_33pasos_3_out_60), .out_93(crono_33pasos_3_out_93), .out_126(crono_33pasos_3_out_126),
    .out_28(crono_33pasos_3_out_28), .out_61(crono_33pasos_3_out_61), .out_94(crono_33pasos_3_out_94),
    .out_127(crono_33pasos_3_out_127), .out_29(crono_33pasos_3_out_29), .out_62(crono_33pasos_3_out_62),
    .out_95(crono_33pasos_3_out_95), .out_128(crono_33pasos_3_out_128), .out_30(crono_33pasos_3_out_30),
    .out_63(crono_33pasos_3_out_63), .out_96(crono_33pasos_3_out_96), .out_129(crono_33pasos_3_out_129),
    .out_31(crono_33pasos_3_out_31), .out_64(crono_33pasos_3_out_64), .out_97(crono_33pasos_3_out_97),
    .out_130(crono_33pasos_3_out_130), .out_32(crono_33pasos_3_out_32), .out_65(crono_33pasos_3_out_65),
    .out_98(crono_33pasos_3_out_98), .out_131(crono_33pasos_3_out_131), .out_33(crono_33pasos_3_out_33),
    .out_66(crono_33pasos_3_out_66), .out_99(crono_33pasos_3_out_99), .out_132(crono_33pasos_3_out_132),
    .out_34(crono_33pasos_3_out_34), .out_67(crono_33pasos_3_out_67), .out_100(crono_33pasos_3_out_100),
    .out_133(crono_33pasos_3_out_133));
  DotMatrix #(.matrixcols(4), .matrixrows(4)) dotmatrix_3 (
    .col0(crono_33pasos_3_out_2), .col1(crono_33pasos_3_out_35), .col2(crono_33pasos_3_out_68),
    .col3(crono_33pasos_3_out_101));
  DotMatrix #(.matrixcols(4), .matrixrows(4)) dotmatrix_4 (
    .col0(crono_33pasos_1_out_4), .col1(crono_33pasos_1_out_37), .col2(crono_33pasos_1_out_70),
    .col3(crono_33pasos_1_out_103));
  DotMatrix #(.matrixcols(4), .matrixrows(4)) dotmatrix_5 (
    .col0(crono_33pasos_1_out_3), .col1(crono_33pasos_1_out_36), .col2(crono_33pasos_1_out_69),
    .col3(crono_33pasos_1_out_102));
  DotMatrix #(.matrixcols(4), .matrixrows(4)) dotmatrix_6 (
    .col0(crono_33pasos_2_out_4), .col1(crono_33pasos_2_out_37), .col2(crono_33pasos_2_out_70),
    .col3(crono_33pasos_2_out_103));
  DotMatrix #(.matrixcols(4), .matrixrows(4)) dotmatrix_7 (
    .col0(crono_33pasos_2_out_3), .col1(crono_33pasos_2_out_36), .col2(crono_33pasos_2_out_69),
    .col3(crono_33pasos_2_out_102));
  DotMatrix #(.matrixcols(4), .matrixrows(4)) dotmatrix_8 (
    .col0(crono_33pasos_3_out_3), .col1(crono_33pasos_3_out_36), .col2(crono_33pasos_3_out_69),
    .col3(crono_33pasos_3_out_102));
  DotMatrix #(.matrixcols(4), .matrixrows(4)) dotmatrix_9 (
    .col0(crono_33pasos_3_out_4), .col1(crono_33pasos_3_out_37), .col2(crono_33pasos_3_out_70),
    .col3(crono_33pasos_3_out_103));
  DotMatrix #(.matrixcols(4), .matrixrows(4)) dotmatrix_10 (
    .col0(crono_33pasos_1_out_5), .col1(crono_33pasos_1_out_38), .col2(crono_33pasos_1_out_71),
    .col3(crono_33pasos_1_out_104));
  DotMatrix #(.matrixcols(4), .matrixrows(4)) dotmatrix_11 (
    .col0(crono_33pasos_1_out_6), .col1(crono_33pasos_1_out_39), .col2(crono_33pasos_1_out_72),
    .col3(crono_33pasos_1_out_105));
  DotMatrix #(.matrixcols(4), .matrixrows(4)) dotmatrix_12 (
    .col0(crono_33pasos_2_out_6), .col1(crono_33pasos_2_out_39), .col2(crono_33pasos_2_out_72),
    .col3(crono_33pasos_2_out_105));
  DotMatrix #(.matrixcols(4), .matrixrows(4)) dotmatrix_13 (
    .col0(crono_33pasos_2_out_5), .col1(crono_33pasos_2_out_38), .col2(crono_33pasos_2_out_71),
    .col3(crono_33pasos_2_out_104));
  DotMatrix #(.matrixcols(4), .matrixrows(4)) dotmatrix_14 (
    .col0(crono_33pasos_3_out_6), .col1(crono_33pasos_3_out_39), .col2(crono_33pasos_3_out_72),
    .col3(crono_33pasos_3_out_105));
  DotMatrix #(.matrixcols(4), .matrixrows(4)) dotmatrix_15 (
    .col0(crono_33pasos_3_out_5), .col1(crono_33pasos_3_out_38), .col2(crono_33pasos_3_out_71),
    .col3(crono_33pasos_3_out_104));
  DotMatrix #(.matrixcols(4), .matrixrows(4)) dotmatrix_16 (
    .col0(crono_33pasos_1_out_8), .col1(crono_33pasos_1_out_41), .col2(crono_33pasos_1_out_74),
    .col3(crono_33pasos_1_out_107));
  DotMatrix #(.matrixcols(4), .matrixrows(4)) dotmatrix_17 (
    .col0(crono_33pasos_1_out_7), .col1(crono_33pasos_1_out_40), .col2(crono_33pasos_1_out_73),
    .col3(crono_33pasos_1_out_106));
  DotMatrix #(.matrixcols(4), .matrixrows(4)) dotmatrix_18 (
    .col0(crono_33pasos_2_out_7), .col1(crono_33pasos_2_out_40), .col2(crono_33pasos_2_out_73),
    .col3(crono_33pasos_2_out_106));
  DotMatrix #(.matrixcols(4), .matrixrows(4)) dotmatrix_19 (
    .col0(crono_33pasos_2_out_8), .col1(crono_33pasos_2_out_41), .col2(crono_33pasos_2_out_74),
    .col3(crono_33pasos_2_out_107));
  DotMatrix #(.matrixcols(4), .matrixrows(4)) dotmatrix_20 (
    .col0(crono_33pasos_3_out_8), .col1(crono_33pasos_3_out_41), .col2(crono_33pasos_3_out_74),
    .col3(crono_33pasos_3_out_107));
  DotMatrix #(.matrixcols(4), .matrixrows(4)) dotmatrix_21 (
    .col0(crono_33pasos_3_out_7), .col1(crono_33pasos_3_out_40), .col2(crono_33pasos_3_out_73),
    .col3(crono_33pasos_3_out_106));
  DotMatrix #(.matrixcols(4), .matrixrows(4)) dotmatrix_22 (
    .col0(crono_33pasos_1_out_9), .col1(crono_33pasos_1_out_42), .col2(crono_33pasos_1_out_75),
    .col3(crono_33pasos_1_out_108));
  DotMatrix #(.matrixcols(4), .matrixrows(4)) dotmatrix_23 (
    .col0(crono_33pasos_1_out_10), .col1(crono_33pasos_1_out_43), .col2(crono_33pasos_1_out_76),
    .col3(crono_33pasos_1_out_109));
  DotMatrix #(.matrixcols(4), .matrixrows(4)) dotmatrix_24 (
    .col0(crono_33pasos_2_out_9), .col1(crono_33pasos_2_out_42), .col2(crono_33pasos_2_out_75),
    .col3(crono_33pasos_2_out_108));
  DotMatrix #(.matrixcols(4), .matrixrows(4)) dotmatrix_25 (
    .col0(crono_33pasos_2_out_10), .col1(crono_33pasos_2_out_43), .col2(crono_33pasos_2_out_76),
    .col3(crono_33pasos_2_out_109));
  DotMatrix #(.matrixcols(4), .matrixrows(4)) dotmatrix_26 (
    .col0(crono_33pasos_3_out_10), .col1(crono_33pasos_3_out_43), .col2(crono_33pasos_3_out_76),
    .col3(crono_33pasos_3_out_109));
  DotMatrix #(.matrixcols(4), .matrixrows(4)) dotmatrix_27 (
    .col0(crono_33pasos_3_out_9), .col1(crono_33pasos_3_out_42), .col2(crono_33pasos_3_out_75),
    .col3(crono_33pasos_3_out_108));
  DotMatrix #(.matrixcols(4), .matrixrows(4)) dotmatrix_28 (
    .col0(crono_33pasos_1_out_11), .col1(crono_33pasos_1_out_44), .col2(crono_33pasos_1_out_77),
    .col3(crono_33pasos_1_out_110));
  DotMatrix #(.matrixcols(4), .matrixrows(4)) dotmatrix_29 (
    .col0(crono_33pasos_1_out_12), .col1(crono_33pasos_1_out_45), .col2(crono_33pasos_1_out_78),
    .col3(crono_33pasos_1_out_111));
  DotMatrix #(.matrixcols(4), .matrixrows(4)) dotmatrix_30 (
    .col0(crono_33pasos_2_out_11), .col1(crono_33pasos_2_out_44), .col2(crono_33pasos_2_out_77),
    .col3(crono_33pasos_2_out_110));
  DotMatrix #(.matrixcols(4), .matrixrows(4)) dotmatrix_31 (
    .col0(crono_33pasos_2_out_12), .col1(crono_33pasos_2_out_45), .col2(crono_33pasos_2_out_78),
    .col3(crono_33pasos_2_out_111));
  DotMatrix #(.matrixcols(4), .matrixrows(4)) dotmatrix_32 (
    .col0(crono_33pasos_3_out_11), .col1(crono_33pasos_3_out_44), .col2(crono_33pasos_3_out_77),
    .col3(crono_33pasos_3_out_110));
  DotMatrix #(.matrixcols(4), .matrixrows(4)) dotmatrix_33 (
    .col0(crono_33pasos_3_out_12), .col1(crono_33pasos_3_out_45), .col2(crono_33pasos_3_out_78),
    .col3(crono_33pasos_3_out_111));
  DotMatrix #(.matrixcols(4), .matrixrows(4)) dotmatrix_34 (
    .col0(crono_33pasos_1_out_13), .col1(crono_33pasos_1_out_46), .col2(crono_33pasos_1_out_79),
    .col3(crono_33pasos_1_out_112));
  DotMatrix #(.matrixcols(4), .matrixrows(4)) dotmatrix_35 (
    .col0(crono_33pasos_1_out_14), .col1(crono_33pasos_1_out_47), .col2(crono_33pasos_1_out_80),
    .col3(crono_33pasos_1_out_113));
  DotMatrix #(.matrixcols(4), .matrixrows(4)) dotmatrix_36 (
    .col0(crono_33pasos_2_out_14), .col1(crono_33pasos_2_out_47), .col2(crono_33pasos_2_out_80),
    .col3(crono_33pasos_2_out_113));
  DotMatrix #(.matrixcols(4), .matrixrows(4)) dotmatrix_37 (
    .col0(crono_33pasos_2_out_13), .col1(crono_33pasos_2_out_46), .col2(crono_33pasos_2_out_79),
    .col3(crono_33pasos_2_out_112));
  DotMatrix #(.matrixcols(4), .matrixrows(4)) dotmatrix_38 (
    .col0(crono_33pasos_3_out_14), .col1(crono_33pasos_3_out_47), .col2(crono_33pasos_3_out_80),
    .col3(crono_33pasos_3_out_113));
  DotMatrix #(.matrixcols(4), .matrixrows(4)) dotmatrix_39 (
    .col0(crono_33pasos_3_out_13), .col1(crono_33pasos_3_out_46), .col2(crono_33pasos_3_out_79),
    .col3(crono_33pasos_3_out_112));
  DotMatrix #(.matrixcols(4), .matrixrows(4)) dotmatrix_40 (
    .col0(crono_33pasos_1_out_16), .col1(crono_33pasos_1_out_49), .col2(crono_33pasos_1_out_82),
    .col3(crono_33pasos_1_out_115));
  DotMatrix #(.matrixcols(4), .matrixrows(4)) dotmatrix_41 (
    .col0(crono_33pasos_1_out_15), .col1(crono_33pasos_1_out_48), .col2(crono_33pasos_1_out_81),
    .col3(crono_33pasos_1_out_114));
  DotMatrix #(.matrixcols(4), .matrixrows(4)) dotmatrix_42 (
    .col0(crono_33pasos_2_out_15), .col1(crono_33pasos_2_out_48), .col2(crono_33pasos_2_out_81),
    .col3(crono_33pasos_2_out_114));
  DotMatrix #(.matrixcols(4), .matrixrows(4)) dotmatrix_43 (
    .col0(crono_33pasos_2_out_16), .col1(crono_33pasos_2_out_49), .col2(crono_33pasos_2_out_82),
    .col3(crono_33pasos_2_out_115));
  DotMatrix #(.matrixcols(4), .matrixrows(4)) dotmatrix_44 (
    .col0(crono_33pasos_3_out_16), .col1(crono_33pasos_3_out_49), .col2(crono_33pasos_3_out_82),
    .col3(crono_33pasos_3_out_115));
  DotMatrix #(.matrixcols(4), .matrixrows(4)) dotmatrix_45 (
    .col0(crono_33pasos_3_out_15), .col1(crono_33pasos_3_out_48), .col2(crono_33pasos_3_out_81),
    .col3(crono_33pasos_3_out_114));
  DotMatrix #(.matrixcols(4), .matrixrows(4)) dotmatrix_46 (
    .col0(crono_33pasos_1_out_18), .col1(crono_33pasos_1_out_51), .col2(crono_33pasos_1_out_84),
    .col3(crono_33pasos_1_out_117));
  DotMatrix #(.matrixcols(4), .matrixrows(4)) dotmatrix_47 (
    .col0(crono_33pasos_1_out_17), .col1(crono_33pasos_1_out_50), .col2(crono_33pasos_1_out_83),
    .col3(crono_33pasos_1_out_116));
  DotMatrix #(.matrixcols(4), .matrixrows(4)) dotmatrix_48 (
    .col0(crono_33pasos_2_out_17), .col1(crono_33pasos_2_out_50), .col2(crono_33pasos_2_out_83),
    .col3(crono_33pasos_2_out_116));
  DotMatrix #(.matrixcols(4), .matrixrows(4)) dotmatrix_49 (
    .col0(crono_33pasos_2_out_18), .col1(crono_33pasos_2_out_51), .col2(crono_33pasos_2_out_84),
    .col3(crono_33pasos_2_out_117));
  DotMatrix #(.matrixcols(4), .matrixrows(4)) dotmatrix_50 (
    .col0(crono_33pasos_3_out_18), .col1(crono_33pasos_3_out_51), .col2(crono_33pasos_3_out_84),
    .col3(crono_33pasos_3_out_117));
  DotMatrix #(.matrixcols(4), .matrixrows(4)) dotmatrix_51 (
    .col0(crono_33pasos_3_out_17), .col1(crono_33pasos_3_out_50), .col2(crono_33pasos_3_out_83),
    .col3(crono_33pasos_3_out_116));
  DotMatrix #(.matrixcols(4), .matrixrows(4)) dotmatrix_52 (
    .col0(crono_33pasos_1_out_20), .col1(crono_33pasos_1_out_53), .col2(crono_33pasos_1_out_86),
    .col3(crono_33pasos_1_out_119));
  DotMatrix #(.matrixcols(4), .matrixrows(4)) dotmatrix_53 (
    .col0(crono_33pasos_1_out_19), .col1(crono_33pasos_1_out_52), .col2(crono_33pasos_1_out_85),
    .col3(crono_33pasos_1_out_118));
  DotMatrix #(.matrixcols(4), .matrixrows(4)) dotmatrix_54 (
    .col0(crono_33pasos_2_out_20), .col1(crono_33pasos_2_out_53), .col2(crono_33pasos_2_out_86),
    .col3(crono_33pasos_2_out_119));
  DotMatrix #(.matrixcols(4), .matrixrows(4)) dotmatrix_55 (
    .col0(crono_33pasos_2_out_19), .col1(crono_33pasos_2_out_52), .col2(crono_33pasos_2_out_85),
    .col3(crono_33pasos_2_out_118));
  DotMatrix #(.matrixcols(4), .matrixrows(4)) dotmatrix_56 (
    .col0(crono_33pasos_3_out_20), .col1(crono_33pasos_3_out_53), .col2(crono_33pasos_3_out_86),
    .col3(crono_33pasos_3_out_119));
  DotMatrix #(.matrixcols(4), .matrixrows(4)) dotmatrix_57 (
    .col0(crono_33pasos_3_out_19), .col1(crono_33pasos_3_out_52), .col2(crono_33pasos_3_out_85),
    .col3(crono_33pasos_3_out_118));
  DotMatrix #(.matrixcols(4), .matrixrows(4)) dotmatrix_58 (
    .col0(crono_33pasos_1_out_21), .col1(crono_33pasos_1_out_54), .col2(crono_33pasos_1_out_87),
    .col3(crono_33pasos_1_out_120));
  DotMatrix #(.matrixcols(4), .matrixrows(4)) dotmatrix_59 (
    .col0(crono_33pasos_1_out_22), .col1(crono_33pasos_1_out_55), .col2(crono_33pasos_1_out_88),
    .col3(crono_33pasos_1_out_121));
  DotMatrix #(.matrixcols(4), .matrixrows(4)) dotmatrix_60 (
    .col0(crono_33pasos_2_out_21), .col1(crono_33pasos_2_out_54), .col2(crono_33pasos_2_out_87),
    .col3(crono_33pasos_2_out_120));
  DotMatrix #(.matrixcols(4), .matrixrows(4)) dotmatrix_61 (
    .col0(crono_33pasos_2_out_22), .col1(crono_33pasos_2_out_55), .col2(crono_33pasos_2_out_88),
    .col3(crono_33pasos_2_out_121));
  DotMatrix #(.matrixcols(4), .matrixrows(4)) dotmatrix_62 (
    .col0(crono_33pasos_3_out_22), .col1(crono_33pasos_3_out_55), .col2(crono_33pasos_3_out_88),
    .col3(crono_33pasos_3_out_121));
  DotMatrix #(.matrixcols(4), .matrixrows(4)) dotmatrix_63 (
    .col0(crono_33pasos_3_out_21), .col1(crono_33pasos_3_out_54), .col2(crono_33pasos_3_out_87),
    .col3(crono_33pasos_3_out_120));
  DotMatrix #(.matrixcols(4), .matrixrows(4)) dotmatrix_64 (
    .col0(crono_33pasos_1_out_23), .col1(crono_33pasos_1_out_56), .col2(crono_33pasos_1_out_89),
    .col3(crono_33pasos_1_out_122));
  DotMatrix #(.matrixcols(4), .matrixrows(4)) dotmatrix_65 (
    .col0(crono_33pasos_1_out_24), .col1(crono_33pasos_1_out_57), .col2(crono_33pasos_1_out_90),
    .col3(crono_33pasos_1_out_123));
  DotMatrix #(.matrixcols(4), .matrixrows(4)) dotmatrix_66 (
    .col0(crono_33pasos_2_out_24), .col1(crono_33pasos_2_out_57), .col2(crono_33pasos_2_out_90),
    .col3(crono_33pasos_2_out_123));
  DotMatrix #(.matrixcols(4), .matrixrows(4)) dotmatrix_67 (
    .col0(crono_33pasos_2_out_23), .col1(crono_33pasos_2_out_56), .col2(crono_33pasos_2_out_89),
    .col3(crono_33pasos_2_out_122));
  DotMatrix #(.matrixcols(4), .matrixrows(4)) dotmatrix_68 (
    .col0(crono_33pasos_3_out_23), .col1(crono_33pasos_3_out_56), .col2(crono_33pasos_3_out_89),
    .col3(crono_33pasos_3_out_122));
  DotMatrix #(.matrixcols(4), .matrixrows(4)) dotmatrix_69 (
    .col0(crono_33pasos_3_out_24), .col1(crono_33pasos_3_out_57), .col2(crono_33pasos_3_out_90),
    .col3(crono_33pasos_3_out_123));
  DotMatrix #(.matrixcols(4), .matrixrows(4)) dotmatrix_70 (
    .col0(crono_33pasos_1_out_26), .col1(crono_33pasos_1_out_59), .col2(crono_33pasos_1_out_92),
    .col3(crono_33pasos_1_out_125));
  DotMatrix #(.matrixcols(4), .matrixrows(4)) dotmatrix_71 (
    .col0(crono_33pasos_1_out_25), .col1(crono_33pasos_1_out_58), .col2(crono_33pasos_1_out_91),
    .col3(crono_33pasos_1_out_124));
  DotMatrix #(.matrixcols(4), .matrixrows(4)) dotmatrix_72 (
    .col0(crono_33pasos_2_out_26), .col1(crono_33pasos_2_out_59), .col2(crono_33pasos_2_out_92),
    .col3(crono_33pasos_2_out_125));
  DotMatrix #(.matrixcols(4), .matrixrows(4)) dotmatrix_73 (
    .col0(crono_33pasos_2_out_25), .col1(crono_33pasos_2_out_58), .col2(crono_33pasos_2_out_91),
    .col3(crono_33pasos_2_out_124));
  DotMatrix #(.matrixcols(4), .matrixrows(4)) dotmatrix_74 (
    .col0(crono_33pasos_3_out_25), .col1(crono_33pasos_3_out_58), .col2(crono_33pasos_3_out_91),
    .col3(crono_33pasos_3_out_124));
  DotMatrix #(.matrixcols(4), .matrixrows(4)) dotmatrix_75 (
    .col0(crono_33pasos_3_out_26), .col1(crono_33pasos_3_out_59), .col2(crono_33pasos_3_out_92),
    .col3(crono_33pasos_3_out_125));
  DotMatrix #(.matrixcols(4), .matrixrows(4)) dotmatrix_76 (
    .col0(crono_33pasos_1_out_27), .col1(crono_33pasos_1_out_60), .col2(crono_33pasos_1_out_93),
    .col3(crono_33pasos_1_out_126));
  DotMatrix #(.matrixcols(4), .matrixrows(4)) dotmatrix_77 (
    .col0(crono_33pasos_1_out_28), .col1(crono_33pasos_1_out_61), .col2(crono_33pasos_1_out_94),
    .col3(crono_33pasos_1_out_127));
  DotMatrix #(.matrixcols(4), .matrixrows(4)) dotmatrix_78 (
    .col0(crono_33pasos_2_out_28), .col1(crono_33pasos_2_out_61), .col2(crono_33pasos_2_out_94),
    .col3(crono_33pasos_2_out_127));
  DotMatrix #(.matrixcols(4), .matrixrows(4)) dotmatrix_79 (
    .col0(crono_33pasos_2_out_27), .col1(crono_33pasos_2_out_60), .col2(crono_33pasos_2_out_93),
    .col3(crono_33pasos_2_out_126));
  DotMatrix #(.matrixcols(4), .matrixrows(4)) dotmatrix_80 (
    .col0(crono_33pasos_3_out_28), .col1(crono_33pasos_3_out_61), .col2(crono_33pasos_3_out_94),
    .col3(crono_33pasos_3_out_127));
  DotMatrix #(.matrixcols(4), .matrixrows(4)) dotmatrix_81 (
    .col0(crono_33pasos_3_out_27), .col1(crono_33pasos_3_out_60), .col2(crono_33pasos_3_out_93),
    .col3(crono_33pasos_3_out_126));
  DotMatrix #(.matrixcols(4), .matrixrows(4)) dotmatrix_82 (
    .col0(crono_33pasos_1_out_30), .col1(crono_33pasos_1_out_63), .col2(crono_33pasos_1_out_96),
    .col3(crono_33pasos_1_out_129));
  DotMatrix #(.matrixcols(4), .matrixrows(4)) dotmatrix_83 (
    .col0(crono_33pasos_1_out_29), .col1(crono_33pasos_1_out_62), .col2(crono_33pasos_1_out_95),
    .col3(crono_33pasos_1_out_128));
  DotMatrix #(.matrixcols(4), .matrixrows(4)) dotmatrix_84 (
    .col0(crono_33pasos_2_out_30), .col1(crono_33pasos_2_out_63), .col2(crono_33pasos_2_out_96),
    .col3(crono_33pasos_2_out_129));
  DotMatrix #(.matrixcols(4), .matrixrows(4)) dotmatrix_85 (
    .col0(crono_33pasos_2_out_29), .col1(crono_33pasos_2_out_62), .col2(crono_33pasos_2_out_95),
    .col3(crono_33pasos_2_out_128));
  DotMatrix #(.matrixcols(4), .matrixrows(4)) dotmatrix_86 (
    .col0(crono_33pasos_3_out_30), .col1(crono_33pasos_3_out_63), .col2(crono_33pasos_3_out_96),
    .col3(crono_33pasos_3_out_129));
  DotMatrix #(.matrixcols(4), .matrixrows(4)) dotmatrix_87 (
    .col0(crono_33pasos_3_out_29), .col1(crono_33pasos_3_out_62), .col2(crono_33pasos_3_out_95),
    .col3(crono_33pasos_3_out_128));
  DotMatrix #(.matrixcols(4), .matrixrows(4)) dotmatrix_88 (
    .col0(crono_33pasos_1_out_31), .col1(crono_33pasos_1_out_64), .col2(crono_33pasos_1_out_97),
    .col3(crono_33pasos_1_out_130));
  DotMatrix #(.matrixcols(4), .matrixrows(4)) dotmatrix_89 (
    .col0(crono_33pasos_1_out_32), .col1(crono_33pasos_1_out_65), .col2(crono_33pasos_1_out_98),
    .col3(crono_33pasos_1_out_131));
  DotMatrix #(.matrixcols(4), .matrixrows(4)) dotmatrix_90 (
    .col0(crono_33pasos_2_out_32), .col1(crono_33pasos_2_out_65), .col2(crono_33pasos_2_out_98),
    .col3(crono_33pasos_2_out_131));
  DotMatrix #(.matrixcols(4), .matrixrows(4)) dotmatrix_91 (
    .col0(crono_33pasos_2_out_31), .col1(crono_33pasos_2_out_64), .col2(crono_33pasos_2_out_97),
    .col3(crono_33pasos_2_out_130));
  DotMatrix #(.matrixcols(4), .matrixrows(4)) dotmatrix_92 (
    .col0(crono_33pasos_3_out_32), .col1(crono_33pasos_3_out_65), .col2(crono_33pasos_3_out_98),
    .col3(crono_33pasos_3_out_131));
  DotMatrix #(.matrixcols(4), .matrixrows(4)) dotmatrix_93 (
    .col0(crono_33pasos_3_out_31), .col1(crono_33pasos_3_out_64), .col2(crono_33pasos_3_out_97),
    .col3(crono_33pasos_3_out_130));
  DotMatrix #(.matrixcols(4), .matrixrows(4)) dotmatrix_94 (
    .col0(crono_33pasos_1_out_33), .col1(crono_33pasos_1_out_66), .col2(crono_33pasos_1_out_99),
    .col3(crono_33pasos_1_out_132));
  DotMatrix #(.matrixcols(4), .matrixrows(4)) dotmatrix_95 (
    .col0(crono_33pasos_1_out_34), .col1(crono_33pasos_1_out_67), .col2(crono_33pasos_1_out_100),
    .col3(crono_33pasos_1_out_133));
  DotMatrix #(.matrixcols(4), .matrixrows(4)) dotmatrix_96 (
    .col0(crono_33pasos_2_out_33), .col1(crono_33pasos_2_out_66), .col2(crono_33pasos_2_out_99),
    .col3(crono_33pasos_2_out_132));
  DotMatrix #(.matrixcols(4), .matrixrows(4)) dotmatrix_97 (
    .col0(crono_33pasos_2_out_34), .col1(crono_33pasos_2_out_67), .col2(crono_33pasos_2_out_100),
    .col3(crono_33pasos_2_out_133));
  DotMatrix #(.matrixcols(4), .matrixrows(4)) dotmatrix_98 (
    .col0(crono_33pasos_3_out_34), .col1(crono_33pasos_3_out_67), .col2(crono_33pasos_3_out_100),
    .col3(crono_33pasos_3_out_133));
  DotMatrix #(.matrixcols(4), .matrixrows(4)) dotmatrix_99 (
    .col0(crono_33pasos_3_out_33), .col1(crono_33pasos_3_out_66), .col2(crono_33pasos_3_out_99),
    .col3(crono_33pasos_3_out_132));

  // Notes on the sheet:
  //   reset
  //   detector dos 1s seguidos
  //   sustituirlo por tu circuito bajo prueba
  //   entrada 
  //   salida
endmodule
