// Logisim project Ampliacion_Secuencial.circ as structural Verilog: 12 circuits, main circuit 7490
module _7490 (
  input  MS1,
  input  MS2,
  input  CP0,
  input  CP1,
  input  MR1,
  input  MR2,
  output Q3,
  output Q2,
  output Q1,
  output Q0
);

  wire and_1_out, and_2_out, and_3_out, j_k_ff_2_qn, or_1_out, or_2_out;

  and and_1 (and_1_out, MR1, MR2);
  T_Flip_Flop #(.trigger("falling")) t_ff_1 (
    .clk(CP0), .T(1'b1), .Q(Q0), .preset(and_2_out), .reset(and_1_out), .en(1'b1));  // open: Qn
  J_K_Flip_Flop #(.trigger("falling")) j_k_ff_1 (
    .J(j_k_ff_2_qn), .clk(CP1), .K(1'b1), .Q(Q1), .preset(1'b0), .en(1'b1), .reset(or_1_out));  // open: Qn
  or or_1 (or_1_out, and_2_out, and_1_out);
  and and_2 (and_2_out, MS1, MS2);
  T_Flip_Flop #(.trigger("falling")) t_ff_2 (
    .clk(Q1), .T(1'b1), .Q(Q2), .preset(1'b0), .reset(or_2_out), .en(1'b1));  // open: Qn
  or or_2 (or_2_out, and_2_out, and_1_out);
  and and_3 (and_3_out, Q1, Q2);
  J_K_Flip_Flop #(.trigger("falling")) j_k_ff_2 (
    .J(and_3_out), .clk(CP1), .K(Q3), .Q(Q3), .Qn(j_k_ff_2_qn), .preset(and_2_out), .en(1'b1),
    .reset(and_1_out));
endmodule

module _7492 (
  input  CP0,
  input  CP1,
  input  MR1,
  input  MR2,
  output Q3,
  output Q2,
  output Q1,
  output Q0
);

  wire and_1_out, j_k_ff_2_qn;

  and and_1 (and_1_out, MR1, MR2);
  T_Flip_Flop #(.trigger("falling")) t_ff_1 (
    .clk(CP0), .T(1'b1), .Q(Q0), .preset(1'b0), .reset(and_1_out), .en(1'b1));  // open: Qn
  J_K_Flip_Flop #(.trigger("falling")) j_k_ff_1 (
    .J(j_k_ff_2_qn), .clk(CP1), .K(1'b1), .Q(Q1), .preset(1'b0), .en(1'b1), .reset(and_1_out));  // open: Qn
  J_K_Flip_Flop #(.trigger("falling")) j_k_ff_2 (
    .J(Q1), .clk(CP1), .K(1'b1), .Q(Q2), .Qn(j_k_ff_2_qn), .preset(1'b0), .en(1'b1), .reset(and_1_out));
  T_Flip_Flop #(.trigger("falling")) t_ff_2 (
    .clk(Q2), .T(1'b1), .Q(Q3), .preset(1'b0), .reset(and_1_out), .en(1'b1));  // open: Qn
endmodule

module _7493 (
  input  CP0,
  input  CP1,
  input  MR1,
  input  MR2,
  output Q3,
  output Q2,
  output Q1,
  output Q0
);

  wire and_1_out;

  and and_1 (and_1_out, MR1, MR2);
  T_Flip_Flop #(.trigger("falling")) t_ff_1 (
    .clk(CP0), .T(1'b1), .Q(Q0), .preset(1'b0), .reset(and_1_out), .en(1'b1));  // open: Qn
  T_Flip_Flop #(.trigger("falling")) t_ff_2 (
    .clk(CP1), .T(1'b1), .Q(Q1), .preset(1'b0), .reset(and_1_out), .en(1'b1));  // open: Qn
  T_Flip_Flop #(.trigger("falling")) t_ff_3 (
    .clk(Q1), .T(1'b1), .Q(Q2), .preset(1'b0), .reset(and_1_out), .en(1'b1));  // open: Qn
  T_Flip_Flop #(.trigger("falling")) t_ff_4 (
    .clk(Q2), .T(1'b1), .Q(Q3), .preset(1'b0), .reset(and_1_out), .en(1'b1));  // open: Qn
endmodule

module _74160 (
  input  PE,
  input  P3,
  input  P2,
  input  P1,
  input  P0,
  input  MR,
  input  CP,
  input  CEP,
  input  CET,
  output TC,
  output Q3,
  output Q2,
  output Q1,
  output Q0
);

  wire and_1_out, and_2_out, and_3_out, and_4_out, and_5_out, and_7_out, and_8_out, and_9_out, and_10_out,
       and_11_out, and_12_out, and_13_out, and_14_out, j_k_ff_4_qn, nand_1_out, nand_2_out, nand_3_out,
       nand_4_out, nand_5_out, nand_6_out, nand_7_out, nand_8_out, not_1_out, not_2_out, not_3_out, or_1_out,
       or_2_out, or_3_out, or_4_out, or_5_out;

  not not_1 (not_1_out, PE);
  not not_2 (not_2_out, MR);
  and and_1 (and_1_out, CEP, CET);
  and and_2 (and_2_out, Q0, and_1_out, j_k_ff_4_qn);
  and and_3 (and_3_out, Q1, Q0, and_1_out);
  and and_4 (and_4_out, Q2, Q1, Q0, and_1_out, 1'b1);
  and and_5 (and_5_out, Q0, and_1_out, Q3);
  and and_6 (TC, Q3, Q0, CET);
  or or_1 (or_1_out, and_4_out, and_5_out);
  nand nand_1 (nand_1_out, not_1_out, nand_2_out);
  nand nand_2 (nand_2_out, P0, not_1_out);
  nand nand_3 (nand_3_out, not_1_out, nand_4_out);
  nand nand_4 (nand_4_out, P1, not_1_out);
  nand nand_5 (nand_5_out, not_1_out, nand_6_out);
  nand nand_6 (nand_6_out, P2, not_1_out);
  nand nand_7 (nand_7_out, not_1_out, nand_8_out);
  nand nand_8 (nand_8_out, P3, not_1_out);
  or or_2 (or_2_out, and_1_out, not_1_out);
  or or_3 (or_3_out, and_2_out, not_1_out);
  or or_4 (or_4_out, and_3_out, not_1_out);
  or or_5 (or_5_out, or_1_out, not_1_out);
  and and_7 (and_7_out, nand_1_out, or_2_out);
  and and_8 (and_8_out, or_2_out, nand_2_out);
  and and_9 (and_9_out, nand_3_out, or_3_out);
  and and_10 (and_10_out, or_3_out, nand_4_out);
  and and_11 (and_11_out, nand_5_out, or_4_out);
  and and_12 (and_12_out, or_4_out, nand_6_out);
  and and_13 (and_13_out, nand_7_out, or_5_out);
  and and_14 (and_14_out, or_5_out, nand_8_out);
  not not_3 (not_3_out, CP);
  J_K_Flip_Flop #(.trigger("falling")) j_k_ff_1 (
    .J(and_7_out), .clk(not_3_out), .K(and_8_out), .Q(Q0), .preset(1'b0), .en(1'b1), .reset(not_2_out));  // open: Qn
  J_K_Flip_Flop #(.trigger("falling")) j_k_ff_2 (
    .J(and_9_out), .clk(not_3_out), .K(and_10_out), .Q(Q1), .preset(1'b0), .en(1'b1), .reset(not_2_out));  // open: Qn
  J_K_Flip_Flop #(.trigger("falling")) j_k_ff_3 (
    .J(and_11_out), .clk(not_3_out), .K(and_12_out), .Q(Q2), .preset(1'b0), .en(1'b1), .reset(not_2_out));  // open: Qn
  J_K_Flip_Flop #(.trigger("falling")) j_k_ff_4 (
    .J(and_13_out), .clk(not_3_out), .K(and_14_out), .Q(Q3), .Qn(j_k_ff_4_qn), .preset(1'b0), .en(1'b1),
    .reset(not_2_out));
endmodule

module _74163 (
  input  PE,
  input  P3,
  input  P2,
  input  P1,
  input  P0,
  input  SR,
  input  CP,
  input  CEP,
  input  CET,
  output TC,
  output Q3,
  output Q2,
  output Q1,
  output Q0
);

  wire and_1_out, and_2_out, and_3_out, and_4_out, and_6_out, and_7_out, and_8_out, and_9_out, and_10_out,
       and_11_out, and_12_out, and_13_out, buffer_1_out, j_k_ff_4_qn, nand_1_out, nand_2_out, nand_3_out,
       nand_4_out, nand_5_out, nand_6_out, nand_7_out, nand_8_out, not_1_out, not_2_out, not_3_out, or_1_out,
       or_2_out, or_3_out, or_4_out, or_5_out;

  buf buffer_1 (buffer_1_out, SR);
  not not_1 (not_1_out, PE);
  or or_1 (or_1_out, not_1_out, not_2_out);
  not not_2 (not_2_out, buffer_1_out);
  and and_1 (and_1_out, CEP, CET);
  and and_2 (and_2_out, Q0, and_1_out);
  and and_3 (and_3_out, Q1, Q0, and_1_out);
  and and_4 (and_4_out, Q2, Q1, Q0, and_1_out, 1'b1);
  and and_5 (TC, Q3, Q2, Q1, Q0, CET);
  nand nand_1 (nand_1_out, or_1_out, nand_2_out);
  nand nand_2 (nand_2_out, P0, buffer_1_out, or_1_out);
  nand nand_3 (nand_3_out, or_1_out, nand_4_out);
  nand nand_4 (nand_4_out, P1, buffer_1_out, or_1_out);
  nand nand_5 (nand_5_out, or_1_out, nand_6_out);
  nand nand_6 (nand_6_out, P2, buffer_1_out, or_1_out);
  nand nand_7 (nand_7_out, or_1_out, nand_8_out);
  nand nand_8 (nand_8_out, P3, buffer_1_out, or_1_out);
  or or_2 (or_2_out, and_1_out, or_1_out);
  or or_3 (or_3_out, and_2_out, or_1_out);
  or or_4 (or_4_out, and_3_out, or_1_out);
  or or_5 (or_5_out, and_4_out, or_1_out);
  and and_6 (and_6_out, nand_1_out, or_2_out);
  and and_7 (and_7_out, or_2_out, nand_2_out);
  and and_8 (and_8_out, nand_3_out, or_3_out);
  and and_9 (and_9_out, or_3_out, nand_4_out);
  and and_10 (and_10_out, nand_5_out, or_4_out);
  and and_11 (and_11_out, or_4_out, nand_6_out);
  and and_12 (and_12_out, nand_7_out, or_5_out);
  and and_13 (and_13_out, or_5_out, nand_8_out);
  not not_3 (not_3_out, CP);
  J_K_Flip_Flop #(.trigger("falling")) j_k_ff_1 (
    .J(and_6_out), .clk(not_3_out), .K(and_7_out), .Q(Q0), .preset(1'b0), .en(1'b1), .reset(1'b0));  // open: Qn
  J_K_Flip_Flop #(.trigger("falling")) j_k_ff_2 (
    .J(and_8_out), .clk(not_3_out), .K(and_9_out), .Q(Q1), .preset(1'b0), .en(1'b1), .reset(1'b0));  // open: Qn
  J_K_Flip_Flop #(.trigger("falling")) j_k_ff_3 (
    .J(and_10_out), .clk(not_3_out), .K(and_11_out), .Q(Q2), .preset(1'b0), .en(1'b1), .reset(1'b0));  // open: Qn
  J_K_Flip_Flop #(.trigger("falling")) j_k_ff_4 (
    .J(and_12_out), .clk(not_3_out), .K(and_13_out), .Q(Q3), .Qn(j_k_ff_4_qn), .preset(1'b0), .en(1'b1),
    .reset(1'b0));
endmodule

module _74164 (
  input  B,
  input  A,
  input  CP,
  input  MR,
  output Q7,
  output Q6,
  output Q5,
  output Q4,
  output Q3,
  output Q2,
  output Q1,
  output Q0
);

  wire and_1_out, not_1_out, not_2_out;

  D_Flip_Flop #(.trigger("falling")) d_ff_1 (
    .clk(not_1_out), .D(and_1_out), .Q(Q0), .preset(1'b0), .en(1'b1), .reset(not_2_out));  // open: Qn
  D_Flip_Flop #(.trigger("falling")) d_ff_2 (
    .clk(not_1_out), .D(Q0), .Q(Q1), .preset(1'b0), .en(1'b1), .reset(not_2_out));  // open: Qn
  D_Flip_Flop #(.trigger("falling")) d_ff_3 (
    .clk(not_1_out), .D(Q1), .Q(Q2), .preset(1'b0), .en(1'b1), .reset(not_2_out));  // open: Qn
  not not_1 (not_1_out, CP);
  D_Flip_Flop #(.trigger("falling")) d_ff_4 (
    .clk(not_1_out), .D(Q2), .Q(Q3), .preset(1'b0), .en(1'b1), .reset(not_2_out));  // open: Qn
  D_Flip_Flop #(.trigger("falling")) d_ff_5 (
    .clk(not_1_out), .D(Q3), .Q(Q4), .preset(1'b0), .en(1'b1), .reset(not_2_out));  // open: Qn
  D_Flip_Flop #(.trigger("falling")) d_ff_6 (
    .clk(not_1_out), .D(Q4), .Q(Q5), .preset(1'b0), .en(1'b1), .reset(not_2_out));  // open: Qn
  and and_1 (and_1_out, B, A);
  D_Flip_Flop #(.trigger("falling")) d_ff_7 (
    .clk(not_1_out), .D(Q5), .Q(Q6), .preset(1'b0), .en(1'b1), .reset(not_2_out));  // open: Qn
  D_Flip_Flop #(.trigger("falling")) d_ff_8 (
    .clk(not_1_out), .D(Q6), .Q(Q7), .preset(1'b0), .en(1'b1), .reset(not_2_out));  // open: Qn
  not not_2 (not_2_out, MR);
endmodule

module _74191 (
  input  U_D,
  input  CE,
  input  CP,
  input  PL,
  input  P3,
  input  P2,
  input  P1,
  input  P0,
  output RC,
  output TC,
  output Q3,
  output Q2,
  output Q1,
  output Q0
);

  wire and_1_out, and_2_out, and_3_out, and_4_out, and_5_out, and_6_out, and_7_out, and_8_out, and_9_out,
       and_10_out, and_11_out, and_12_out, j_k_ff_1_qn, j_k_ff_2_qn, j_k_ff_3_qn, j_k_ff_4_qn, nand_2_out,
       nand_3_out, nand_4_out, nand_5_out, nor_1_out, nor_2_out, not_1_out, not_2_out, not_3_out, not_4_out,
       not_5_out, not_6_out, not_7_out, not_8_out, not_9_out, or_2_out, or_3_out, or_4_out;

  not not_1 (not_1_out, U_D);
  not not_2 (not_2_out, CP);
  and and_1 (and_1_out, not_1_out, Q0, Q1, Q2, Q3);
  nand nand_1 (RC, not_2_out, not_4_out, TC);
  not not_3 (not_3_out, not_1_out);
  and and_2 (and_2_out, not_3_out, j_k_ff_1_qn, j_k_ff_2_qn, j_k_ff_3_qn, j_k_ff_4_qn);
  or or_1 (TC, and_1_out, and_2_out);
  nor nor_1 (nor_1_out, not_3_out, CE);
  not not_4 (not_4_out, CE);
  nand nand_2 (nand_2_out, P0, not_9_out);
  not not_5 (not_5_out, nand_2_out);
  nor nor_2 (nor_2_out, CE, not_1_out);
  and and_3 (and_3_out, nand_2_out, not_9_out);
  J_K_Flip_Flop #(.trigger("falling")) j_k_ff_1 (
    .J(not_4_out), .clk(not_2_out), .K(not_4_out), .Q(Q0), .Qn(j_k_ff_1_qn), .preset(not_5_out), .en(1'b1),
    .reset(and_3_out));
  and and_4 (and_4_out, nor_2_out, j_k_ff_1_qn);
  nand nand_3 (nand_3_out, P1, not_9_out);
  not not_6 (not_6_out, nand_3_out);
  and and_5 (and_5_out, Q0, nor_1_out);
  or or_2 (or_2_out, and_4_out, and_5_out);
  J_K_Flip_Flop #(.trigger("falling")) j_k_ff_2 (
    .J(or_2_out), .clk(not_2_out), .K(or_2_out), .Q(Q1), .Qn(j_k_ff_2_qn), .preset(not_6_out), .en(1'b1),
    .reset(and_6_out));
  nand nand_4 (nand_4_out, P2, not_9_out);
  not not_7 (not_7_out, nand_4_out);
  and and_6 (and_6_out, nand_3_out, not_9_out);
  and and_7 (and_7_out, Q0, Q1, nor_1_out);
  and and_8 (and_8_out, nor_2_out, j_k_ff_1_qn, j_k_ff_2_qn);
  or or_3 (or_3_out, and_8_out, and_7_out);
  nand nand_5 (nand_5_out, P3, not_9_out);
  not not_8 (not_8_out, nand_5_out);
  and and_9 (and_9_out, nand_4_out, not_9_out);
  J_K_Flip_Flop #(.trigger("falling")) j_k_ff_3 (
    .J(or_3_out), .clk(not_2_out), .K(or_3_out), .Q(Q2), .Qn(j_k_ff_3_qn), .preset(not_7_out), .en(1'b1),
    .reset(and_9_out));
  and and_10 (and_10_out, nor_2_out, j_k_ff_1_qn, j_k_ff_2_qn, j_k_ff_3_qn, 1'b1);
  and and_11 (and_11_out, 1'b1, Q0, Q1, Q2, nor_1_out);
  and and_12 (and_12_out, nand_5_out, not_9_out);
  or or_4 (or_4_out, and_10_out, and_11_out);
  J_K_Flip_Flop #(.trigger("falling")) j_k_ff_4 (
    .J(or_4_out), .clk(not_2_out), .K(or_4_out), .Q(Q3), .Qn(j_k_ff_4_qn), .preset(not_8_out), .en(1'b1),
    .reset(and_12_out));
  not not_9 (not_9_out, PL);
endmodule

module _74192 (
  input  PL,
  input  P3,
  input  P2,
  input  P1,
  input  P0,
  input  CPU,
  input  CPD,
  input  MR,
  output TCU,
  output TCD,
  output Q3,
  output Q2,
  output Q1,
  output Q0
);

  wire and_1_out, and_2_out, and_3_out, and_4_out, and_5_out, and_6_out, and_7_out, buffer_1_out,
       buffer_2_out, nand_3_out, nand_4_out, nand_5_out, nand_6_out, nand_7_out, nand_8_out, nand_9_out,
       nand_10_out, nand_11_out, nand_12_out, nand_13_out, nand_14_out, nand_15_out, nor_1_out, nor_2_out,
       nor_3_out, nor_4_out, not_1_out, not_2_out, not_3_out, not_4_out, not_5_out, not_6_out, not_7_out,
       not_8_out, t_ff_1_qn, t_ff_2_qn, t_ff_3_qn, t_ff_4_qn;

  nand nand_1 (TCU, not_7_out, Q0, Q3);
  buf buffer_1 (buffer_1_out, not_7_out);
  buf buffer_2 (buffer_2_out, not_8_out);
  nand nand_2 (TCD, t_ff_4_qn, t_ff_3_qn, t_ff_2_qn, t_ff_1_qn, not_8_out);
  not not_1 (not_1_out, nand_3_out);
  nor nor_1 (nor_1_out, buffer_1_out, buffer_2_out);
  not not_2 (not_2_out, PL);
  nand nand_3 (nand_3_out, not_2_out, not_3_out, P0);
  nand nand_4 (nand_4_out, nand_3_out, not_2_out);
  T_Flip_Flop t_ff_1 (
    .clk(nor_1_out), .T(1'b1), .Q(Q0), .Qn(t_ff_1_qn), .preset(not_1_out), .reset(nand_5_out), .en(1'b1));
  nand nand_5 (nand_5_out, not_3_out, nand_4_out);
  not not_3 (not_3_out, MR);
  and and_1 (and_1_out, not_7_out, t_ff_4_qn, Q0);
  not not_4 (not_4_out, nand_6_out);
  nor nor_2 (nor_2_out, and_1_out, and_2_out);
  and and_2 (and_2_out, t_ff_1_qn, not_8_out, nand_9_out);
  nand nand_6 (nand_6_out, not_2_out, not_3_out, P1);
  nand nand_7 (nand_7_out, nand_6_out, not_2_out);
  T_Flip_Flop t_ff_2 (
    .clk(nor_2_out), .T(1'b1), .Q(Q1), .Qn(t_ff_2_qn), .preset(not_4_out), .reset(nand_8_out), .en(1'b1));
  nand nand_8 (nand_8_out, not_3_out, nand_7_out);
  and and_3 (and_3_out, not_7_out, Q0, Q1);
  and and_4 (and_4_out, t_ff_2_qn, t_ff_1_qn, not_8_out, nand_9_out, 1'b1);
  nand nand_9 (nand_9_out, t_ff_2_qn, t_ff_3_qn, t_ff_4_qn);
  nand nand_10 (nand_10_out, not_2_out, not_3_out, P2);
  not not_5 (not_5_out, nand_10_out);
  nor nor_3 (nor_3_out, and_3_out, and_4_out);
  nand nand_11 (nand_11_out, nand_10_out, not_2_out);
  T_Flip_Flop t_ff_3 (
    .clk(nor_3_out), .T(1'b1), .Q(Q2), .Qn(t_ff_3_qn), .preset(not_5_out), .reset(nand_12_out), .en(1'b1));
  nand nand_12 (nand_12_out, not_3_out, nand_11_out);
  and and_5 (and_5_out, not_7_out, Q0, Q1, Q2, 1'b1);
  and and_6 (and_6_out, not_7_out, Q0, Q3);
  and and_7 (and_7_out, t_ff_3_qn, t_ff_2_qn, t_ff_1_qn, not_8_out, 1'b1);
  nand nand_13 (nand_13_out, not_2_out, not_3_out, P3);
  not not_6 (not_6_out, nand_13_out);
  nor nor_4 (nor_4_out, and_5_out, and_6_out, and_7_out);
  nand nand_14 (nand_14_out, not_3_out, nand_15_out);
  not not_7 (not_7_out, CPU);
  nand nand_15 (nand_15_out, nand_13_out, not_2_out);
  T_Flip_Flop t_ff_4 (
    .clk(nor_4_out), .T(1'b1), .Q(Q3), .Qn(t_ff_4_qn), .preset(not_6_out), .reset(nand_14_out), .en(1'b1));
  not not_8 (not_8_out, CPD);
endmodule

module _74165 (
  input  PL,
  input  P7,
  input  P6,
  input  P5,
  input  P4,
  input  P3,
  input  P2,
  input  P1,
  input  P0,
  input  DS,
  input  CP1,
  input  CP2,
  output nQ7,
  output Q7
);

  wire and_1_out, and_2_out, and_3_out, and_4_out, and_5_out, and_6_out, and_7_out, and_8_out, and_9_out,
       and_10_out, nand_1_out, nand_2_out, nand_3_out, nand_4_out, nand_5_out, nand_6_out, nand_7_out,
       nand_8_out, nor_1_out, not_1_out, not_2_out, not_3_out, not_4_out, not_5_out, not_6_out, not_7_out,
       not_8_out, not_9_out, not_10_out, not_11_out, s_r_ff_1_q, s_r_ff_1_qn, s_r_ff_2_q, s_r_ff_2_qn,
       s_r_ff_3_q, s_r_ff_3_qn, s_r_ff_4_q, s_r_ff_4_qn, s_r_ff_5_q, s_r_ff_5_qn, s_r_ff_6_q, s_r_ff_6_qn,
       s_r_ff_7_q, s_r_ff_7_qn;

  not not_1 (not_1_out, not_2_out);
  not not_2 (not_2_out, DS);
  S_R_Flip_Flop #(.trigger("falling")) s_r_ff_1 (
    .S(not_1_out), .clk(nor_1_out), .R(not_2_out), .Q(s_r_ff_1_q), .Qn(s_r_ff_1_qn), .preset(not_3_out),
    .reset(and_1_out), .en(1'b1));
  not not_3 (not_3_out, nand_1_out);
  and and_1 (and_1_out, nand_1_out, not_4_out);
  nand nand_1 (nand_1_out, not_4_out, P0);
  not not_4 (not_4_out, PL);
  S_R_Flip_Flop #(.trigger("falling")) s_r_ff_2 (
    .S(s_r_ff_1_q), .clk(nor_1_out), .R(s_r_ff_1_qn), .Q(s_r_ff_2_q), .Qn(s_r_ff_2_qn), .preset(not_5_out),
    .reset(and_2_out), .en(1'b1));
  not not_5 (not_5_out, nand_2_out);
  and and_2 (and_2_out, nand_2_out, not_4_out);
  nand nand_2 (nand_2_out, not_4_out, P1);
  S_R_Flip_Flop #(.trigger("falling")) s_r_ff_3 (
    .S(s_r_ff_2_q), .clk(nor_1_out), .R(s_r_ff_2_qn), .Q(s_r_ff_3_q), .Qn(s_r_ff_3_qn), .preset(not_6_out),
    .reset(and_3_out), .en(1'b1));
  and and_3 (and_3_out, nand_3_out, not_4_out);
  not not_6 (not_6_out, nand_3_out);
  nand nand_3 (nand_3_out, not_4_out, P2);
  S_R_Flip_Flop #(.trigger("falling")) s_r_ff_4 (
    .S(s_r_ff_3_q), .clk(nor_1_out), .R(s_r_ff_3_qn), .Q(s_r_ff_4_q), .Qn(s_r_ff_4_qn), .preset(not_7_out),
    .reset(and_4_out), .en(1'b1));
  not not_7 (not_7_out, nand_4_out);
  nand nand_4 (nand_4_out, not_4_out, P3);
  and and_4 (and_4_out, nand_4_out, not_4_out);
  not not_8 (not_8_out, nand_5_out);
  nand nand_5 (nand_5_out, not_4_out, P4);
  S_R_Flip_Flop #(.trigger("falling")) s_r_ff_5 (
    .S(s_r_ff_4_q), .clk(nor_1_out), .R(s_r_ff_4_qn), .Q(s_r_ff_5_q), .Qn(s_r_ff_5_qn), .preset(not_8_out),
    .reset(and_5_out), .en(1'b1));
  and and_5 (and_5_out, nand_5_out, not_4_out);
  not not_9 (not_9_out, nand_6_out);
  nand nand_6 (nand_6_out, not_4_out, P5);
  S_R_Flip_Flop #(.trigger("falling")) s_r_ff_6 (
    .S(s_r_ff_5_q), .clk(nor_1_out), .R(s_r_ff_5_qn), .Q(s_r_ff_6_q), .Qn(s_r_ff_6_qn), .preset(not_9_out),
    .reset(and_6_out), .en(1'b1));
  buf and_6 (and_6_out, not_4_out);  // AND_Gate
  not not_10 (not_10_out, nand_7_out);
  nand nand_7 (nand_7_out, not_4_out, P6);
  S_R_Flip_Flop #(.trigger("falling")) s_r_ff_7 (
    .S(s_r_ff_6_q), .clk(nor_1_out), .R(s_r_ff_6_qn), .Q(s_r_ff_7_q), .Qn(s_r_ff_7_qn), .preset(not_10_out),
    .reset(and_7_out), .en(1'b1));
  and and_7 (and_7_out, nand_7_out, not_4_out);
  not not_11 (not_11_out, nand_8_out);
  nand nand_8 (nand_8_out, not_4_out, P7);
  nor nor_1 (nor_1_out, and_9_out, and_10_out);
  S_R_Flip_Flop #(.trigger("falling")) s_r_ff_8 (
    .S(s_r_ff_7_q), .clk(nor_1_out), .R(s_r_ff_7_qn), .Q(Q7), .Qn(nQ7), .preset(not_11_out),
    .reset(and_8_out), .en(1'b1));
  and and_8 (and_8_out, nand_8_out, not_4_out);
  and and_9 (and_9_out, CP1, PL);
  and and_10 (and_10_out, CP2, PL);
endmodule

module _74166 (
  input  CL,
  input  SER_IN,
  input  CLK,
  input  CLK_I,
  input  S_L,
  input  H,
  input  G,
  input  F,
  input  E,
  input  D,
  input  C,
  input  B,
  input  A,
  output QH
);

  wire and_1_out, and_2_out, and_3_out, and_4_out, and_5_out, and_6_out, and_7_out, and_8_out, and_9_out,
       and_10_out, and_11_out, and_12_out, and_13_out, and_14_out, and_15_out, and_16_out, nor_1_out,
       nor_2_out, nor_3_out, nor_4_out, nor_5_out, nor_6_out, nor_7_out, nor_8_out, nor_9_out, not_1_out,
       not_2_out, not_3_out, not_4_out, not_5_out, not_6_out, not_7_out, not_8_out, not_9_out, not_10_out,
       not_11_out, s_r_ff_1_q, s_r_ff_2_q, s_r_ff_3_q, s_r_ff_4_q, s_r_ff_5_q, s_r_ff_6_q, s_r_ff_7_q;

  not not_1 (not_1_out, S_L);
  and and_1 (and_1_out, SER_IN, not_2_out);
  not not_2 (not_2_out, not_1_out);
  and and_2 (and_2_out, not_1_out, A);
  and and_3 (and_3_out, s_r_ff_1_q, not_2_out);
  and and_4 (and_4_out, not_1_out, B);
  and and_5 (and_5_out, s_r_ff_2_q, not_2_out);
  and and_6 (and_6_out, not_1_out, C);
  and and_7 (and_7_out, s_r_ff_3_q, not_2_out);
  and and_8 (and_8_out, not_1_out, D);
  and and_9 (and_9_out, s_r_ff_4_q, not_2_out);
  and and_10 (and_10_out, not_1_out, E);
  and and_11 (and_11_out, s_r_ff_5_q, not_2_out);
  and and_12 (and_12_out, not_1_out, F);
  and and_13 (and_13_out, s_r_ff_6_q, not_2_out);
  and and_14 (and_14_out, not_1_out, G);
  and and_15 (and_15_out, s_r_ff_7_q, not_2_out);
  and and_16 (and_16_out, not_1_out, H);
  nor nor_1 (nor_1_out, and_1_out, and_2_out);
  nor nor_2 (nor_2_out, and_3_out, and_4_out);
  nor nor_3 (nor_3_out, and_5_out, and_6_out);
  nor nor_4 (nor_4_out, and_7_out, and_8_out);
  nor nor_5 (nor_5_out, and_9_out, and_10_out);
  nor nor_6 (nor_6_out, and_11_out, and_12_out);
  nor nor_7 (nor_7_out, and_13_out, and_14_out);
  nor nor_8 (nor_8_out, and_15_out, and_16_out);
  not not_3 (not_3_out, CL);
  nor nor_9 (nor_9_out, CLK, CLK_I);
  not not_4 (not_4_out, nor_1_out);
  not not_5 (not_5_out, nor_2_out);
  not not_6 (not_6_out, nor_3_out);
  not not_7 (not_7_out, nor_4_out);
  not not_8 (not_8_out, nor_5_out);
  not not_9 (not_9_out, nor_6_out);
  not not_10 (not_10_out, nor_7_out);
  not not_11 (not_11_out, nor_8_out);
  S_R_Flip_Flop s_r_ff_1 (
    .S(not_4_out), .clk(nor_9_out), .R(nor_1_out), .Q(s_r_ff_1_q), .preset(1'b0), .en(1'b1));  // open: Qn, reset
  S_R_Flip_Flop s_r_ff_2 (
    .S(not_5_out), .clk(nor_9_out), .R(nor_2_out), .Q(s_r_ff_2_q), .preset(1'b0), .en(1'b1));  // open: Qn, reset
  S_R_Flip_Flop s_r_ff_3 (
    .S(not_6_out), .clk(nor_9_out), .R(nor_3_out), .Q(s_r_ff_3_q), .preset(1'b0), .en(1'b1));  // open: Qn, reset
  S_R_Flip_Flop s_r_ff_4 (
    .S(not_7_out), .clk(nor_9_out), .R(nor_4_out), .Q(s_r_ff_4_q), .preset(1'b0), .en(1'b1));  // open: Qn, reset
  S_R_Flip_Flop s_r_ff_5 (
    .S(not_8_out), .clk(nor_9_out), .R(nor_5_out), .Q(s_r_ff_5_q), .preset(1'b0), .en(1'b1));  // open: Qn, reset
  S_R_Flip_Flop s_r_ff_6 (
    .S(not_9_out), .clk(nor_9_out), .R(nor_6_out), .Q(s_r_ff_6_q), .preset(1'b0), .en(1'b1));  // open: Qn, reset
  S_R_Flip_Flop s_r_ff_7 (
    .S(not_10_out), .clk(nor_9_out), .R(nor_7_out), .Q(s_r_ff_7_q), .preset(1'b0), .reset(not_3_out),
    .en(1'b1));  // open: Qn
  S_R_Flip_Flop s_r_ff_8 (
    .S(not_11_out), .clk(nor_9_out), .R(nor_8_out), .Q(QH), .preset(1'b0), .reset(not_3_out), .en(1'b1));  // open: Qn
endmodule

module _74194 (
  input  S1,
  input  S0,
  input  P3,
  input  P2,
  input  P1,
  input  P0,
  input  DSR,
  input  DSL,
  input  CP,
  input  MR,
  output Q3,
  output Q2,
  output Q1,
  output Q0
);

  wire and_1_out, and_2_out, and_3_out, and_4_out, and_5_out, and_6_out, and_7_out, and_8_out, and_9_out,
       and_10_out, and_11_out, and_12_out, and_13_out, and_14_out, and_15_out, and_16_out, nor_1_out,
       nor_2_out, nor_3_out, nor_4_out, not_1_out, not_2_out, not_3_out, not_4_out, not_5_out, not_6_out,
       not_7_out, not_8_out, not_9_out, not_10_out, not_11_out, not_12_out, not_13_out;

  not not_1 (not_1_out, not_2_out);
  not not_2 (not_2_out, S1);
  and and_1 (and_1_out, DSR, not_2_out, not_5_out);
  and and_2 (and_2_out, not_5_out, not_1_out, P0);
  and and_3 (and_3_out, not_4_out, not_1_out, Q1);
  nor nor_1 (nor_1_out, 1'b0, and_1_out, and_2_out, and_3_out, and_4_out);
  not not_3 (not_3_out, nor_1_out);
  not not_4 (not_4_out, S0);
  not not_5 (not_5_out, not_4_out);
  and and_4 (and_4_out, not_4_out, not_2_out, Q0);
  and and_5 (and_5_out, Q0, not_2_out, not_5_out);
  S_R_Flip_Flop #(.trigger("falling")) s_r_ff_1 (
    .S(not_3_out), .clk(not_13_out), .R(nor_1_out), .Q(Q0), .preset(1'b0), .reset(not_6_out), .en(1'b1));  // open: Qn
  not not_6 (not_6_out, MR);
  and and_6 (and_6_out, not_4_out, not_1_out, Q2);
  and and_7 (and_7_out, not_5_out, not_1_out, P1);
  nor nor_2 (nor_2_out, 1'b0, and_5_out, and_7_out, and_6_out, and_8_out);
  not not_7 (not_7_out, nor_2_out);
  and and_8 (and_8_out, not_4_out, not_2_out, Q1);
  S_R_Flip_Flop #(.trigger("falling")) s_r_ff_2 (
    .S(not_7_out), .clk(not_13_out), .R(nor_2_out), .Q(Q1), .preset(1'b0), .reset(not_8_out), .en(1'b1));  // open: Qn
  not not_8 (not_8_out, MR);
  and and_9 (and_9_out, not_5_out, not_1_out, P2);
  and and_10 (and_10_out, Q1, not_2_out, not_5_out);
  nor nor_3 (nor_3_out, 1'b0, and_10_out, and_9_out, and_11_out, and_12_out);
  and and_11 (and_11_out, not_4_out, not_1_out, Q3);
  and and_12 (and_12_out, not_4_out, not_2_out, Q2);
  S_R_Flip_Flop #(.trigger("falling")) s_r_ff_3 (
    .S(not_9_out), .clk(not_13_out), .R(nor_3_out), .Q(Q2), .preset(1'b0), .reset(not_10_out), .en(1'b1));  // open: Qn
  not not_9 (not_9_out, nor_3_out);
  not not_10 (not_10_out, MR);
  and and_13 (and_13_out, not_5_out, not_1_out, P3);
  and and_14 (and_14_out, Q2, not_2_out, not_5_out);
  and and_15 (and_15_out, not_4_out, not_1_out, DSL);
  and and_16 (and_16_out, not_4_out, not_2_out, Q3);
  nor nor_4 (nor_4_out, 1'b0, and_14_out, and_13_out, and_15_out, and_16_out);
  not not_11 (not_11_out, nor_4_out);
  not not_12 (not_12_out, MR);
  not not_13 (not_13_out, CP);
  S_R_Flip_Flop #(.trigger("falling")) s_r_ff_4 (
    .S(not_11_out), .clk(not_13_out), .R(nor_4_out), .Q(Q3), .preset(1'b0), .reset(not_12_out), .en(1'b1));  // open: Qn
endmodule

module _74195 (
  input  J,
  input  nK,
  input  PE,
  input  P3,
  input  P2,
  input  P1,
  input  P0,
  input  CP,
  input  MR,
  output nQ3,
  output Q3,
  output Q2,
  output Q1,
  output Q0
);

  wire and_1_out, and_2_out, and_3_out, and_4_out, and_5_out, and_6_out, and_7_out, and_8_out, and_9_out,
       nor_1_out, nor_2_out, nor_3_out, nor_4_out, not_1_out, not_2_out, not_3_out, not_4_out, not_5_out,
       not_6_out, not_7_out, not_8_out, s_r_ff_1_qn;

  not not_1 (not_1_out, PE);
  not not_2 (not_2_out, not_1_out);
  and and_1 (and_1_out, s_r_ff_1_qn, J, not_2_out);
  and and_2 (and_2_out, not_1_out, P0);
  and and_3 (and_3_out, not_2_out, nK, Q0);
  nor nor_1 (nor_1_out, and_1_out, and_3_out, and_2_out);
  not not_3 (not_3_out, nor_1_out);
  not not_4 (not_4_out, MR);
  and and_4 (and_4_out, Q0, not_2_out);
  S_R_Flip_Flop #(.trigger("falling")) s_r_ff_1 (
    .S(not_3_out), .clk(not_8_out), .R(nor_1_out), .Q(Q0), .Qn(s_r_ff_1_qn), .preset(1'b0),
    .reset(not_4_out), .en(1'b1));
  and and_5 (and_5_out, not_1_out, P1);
  nor nor_2 (nor_2_out, and_4_out, and_5_out);
  not not_5 (not_5_out, nor_2_out);
  and and_6 (and_6_out, Q1, not_2_out);
  nor nor_3 (nor_3_out, and_6_out, and_7_out);
  S_R_Flip_Flop #(.trigger("falling")) s_r_ff_2 (
    .S(not_5_out), .clk(not_8_out), .R(nor_2_out), .Q(Q1), .preset(1'b0), .reset(not_4_out), .en(1'b1));  // open: Qn
  and and_7 (and_7_out, not_1_out, P2);
  not not_6 (not_6_out, nor_3_out);
  S_R_Flip_Flop #(.trigger("falling")) s_r_ff_3 (
    .S(not_6_out), .clk(not_8_out), .R(nor_3_out), .Q(Q2), .preset(1'b0), .reset(not_4_out), .en(1'b1));  // open: Qn
  and and_8 (and_8_out, not_1_out, P3);
  and and_9 (and_9_out, Q2, not_2_out);
  nor nor_4 (nor_4_out, and_9_out, and_8_out);
  not not_7 (not_7_out, nor_4_out);
  not not_8 (not_8_out, CP);
  S_R_Flip_Flop #(.trigger("falling")) s_r_ff_4 (
    .S(not_7_out), .clk(not_8_out), .R(nor_4_out), .Q(Q3), .Qn(nQ3), .preset(1'b0), .reset(not_4_out),
    .en(1'b1));
endmodule
